// Logisim project success.circ as structural Verilog: 12 circuits, main circuit PLAYER
module RISCV (
  input  IRA,
  input  IRB,
  input  IRC,
  input  IRD,
  input  IRE,
  input  IRF,
  input  CLK,
  input  RST,
  input  GO,
  output [31:0] R1,
  output [31:0] R2,
  output [31:0] R3,
  output [31:0] R4,
  output [31:0] LEDDATA,
  output [31:0] R5,
  output [31:0] R6,
  output [31:0] R7,
  output [31:0] R8,
  output [31:0] R9,
  output [31:0] R10,
  output [31:0] R11,
  output [31:0] R12,
  output [31:0] R13,
  output [31:0] R14,
  output [31:0] R15,
  output [31:0] R16,
  output [31:0] R17,
  output [31:0] R18,
  output [31:0] R19,
  output [31:0] R20,
  output [31:0] R21,
  output [31:0] R22,
  output [31:0] R23,
  output [31:0] R24,
  output [31:0] R25,
  output [31:0] R26,
  output [31:0] R27,
  output [31:0] R28,
  output [31:0] R29,
  output [31:0] R30,
  output [31:0] R31,
  output [31:0] R32
);

  wire alu_1_equal, alu_1_less, and_1_out, and_2_out, and_3_out, and_4_out, and_5_out, and_6_out, and_10_out,
       and_11_out, and_12_out, and_15_out, B, CLK_t, CLR1, CLR2, CLR3, CLR4, CLR5, CLR6, comparator_2_eq,
       comparator_3_gt, controller_1_alu_src, controller_1_beq, controller_1_bne, controller_1_memtoreg,
       controller_1_s_type, d_ff_1_q, d_ff_2_q, d_ff_3_q, d_ff_4_q, d_ff_5_q, d_ff_6_q, ecall, half, halt,
       IE, INTR, INTR1, INTR2, INTR3, INTR4, INTR5, INTR6, IRHAVE, J, jal, jalr, led, lui, MemWrite,
       not_1_out, not_2_out, not_3_out, not_4_out, not_5_out, not_6_out, or_7_out, or_8_out, or_9_out,
       or_10_out, or_11_out, or_12_out, or_14_out, or_15_out, or_17_out, or_18_out, or_20_out, RegWrite,
       uret, W1, W2, W3, W4, W5, W6;
  wire [1:0] priority_encoder_2_out, priority_encoder_3_out;
  wire [2:0] priority_encoder_1_out, register_1_q;
  wire [3:0] controller_1_alu_op;
  wire [4:0] multiplexer_3_out, multiplexer_5_out;
  wire [9:0] ADDR;
  wire [11:0] multiplexer_4_out;
  wire [15:0] TOTALTIME;
  wire [31:0] adder_1_out, adder_2_out, adder_3_out, aluresult, and_8_out, and_9_out, bit_extender_1_out,
       bit_extender_2_out, bit_extender_3_out, bit_extender_4_out, DATAPLACE_data, IR, IR_PC, luidata,
       mazemap_1_r1, mazemap_1_r2, mazemap_1_r3, mazemap_1_r4, mazemap_1_r5, mazemap_1_r6, mazemap_1_r7,
       mazemap_1_r8, mazemap_1_r9, mazemap_1_r10, mazemap_1_r11, mazemap_1_r12, mazemap_1_r13, mazemap_1_r14,
       mazemap_1_r15, mazemap_1_r16, mazemap_1_r17, mazemap_1_r18, mazemap_1_r19, mazemap_1_r20,
       mazemap_1_r21, mazemap_1_r22, mazemap_1_r23, mazemap_1_r24, mazemap_1_r25, mazemap_1_r26,
       mazemap_1_r27, mazemap_1_r28, mazemap_1_r29, mazemap_1_r30, mazemap_1_r31, mazemap_1_r32, MDin, MEPC,
       multiplexer_2_out, multiplexer_6_out, multiplexer_7_out, multiplexer_8_out, multiplexer_9_out,
       multiplexer_11_out, multiplexer_12_out, PC, RDin, regifile_1_r1, result, shifter_2_out, shifter_3_out,
       shifter_4_out;

  D_Flip_Flop #(.trigger("rising"), .Pre_Clr_Positions("LEGACY"), .NegatePresetClear("false"), .enable("true"), .NewFFLayout("false")) d_ff_1 (
    .clk(IRA), .D(1'b1), .Q(d_ff_1_q), .preset(1'b0), .en(1'b1), .reset(INTR1));  // open: Qn
  or or_1 (W1, INTR1, d_ff_1_q);
  D_Flip_Flop #(.trigger("rising"), .Pre_Clr_Positions("LEGACY"), .NegatePresetClear("false"), .enable("true"), .NewFFLayout("false")) d_ff_2 (
    .clk(IRB), .D(1'b1), .Q(d_ff_2_q), .preset(1'b0), .en(1'b1), .reset(INTR2));  // open: Qn
  or or_2 (W2, INTR2, d_ff_2_q);
  or or_3 (W3, INTR3, d_ff_3_q);
  or or_4 (W4, INTR4, d_ff_4_q);
  or or_5 (W5, INTR5, d_ff_5_q);
  or or_6 (W6, INTR6, d_ff_6_q);
  Multiplexer #(.select(3), .width(32), .disabled(0), .enable("false")) multiplexer_1 (
    .in0({32{1'b0}}), .in1(32'h400444), .in2(32'h4003dc), .in3(32'h40032c), .in4(32'h400384),
    .in5(32'h400004), .in6(32'h400198), .in7({32{1'b0}}), .out(IR_PC), .sel(priority_encoder_1_out));
  Priority_Encoder #(.select(3), .disabled(0)) priority_encoder_1 (
    .in0(1'b1), .in1(INTR1), .in2(INTR2), .in3(INTR3), .in4(INTR4), .in5(INTR5), .in6(INTR6), .in7(1'b0),
    .out(priority_encoder_1_out), .en_in(1'b1));  // open: gs, en_out
  D_Flip_Flop #(.trigger("rising"), .Pre_Clr_Positions("LEGACY"), .NegatePresetClear("false"), .enable("true"), .NewFFLayout("false")) d_ff_3 (
    .clk(IRC), .D(1'b1), .Q(d_ff_3_q), .preset(1'b0), .en(1'b1), .reset(INTR3));  // open: Qn
  D_Flip_Flop #(.trigger("rising"), .Pre_Clr_Positions("LEGACY"), .NegatePresetClear("false"), .enable("true"), .NewFFLayout("false")) d_ff_4 (
    .clk(IRD), .D(1'b1), .Q(d_ff_4_q), .preset(1'b0), .en(1'b1), .reset(INTR4));  // open: Qn
  D_Flip_Flop #(.trigger("rising"), .Pre_Clr_Positions("LEGACY"), .NegatePresetClear("false"), .enable("true"), .NewFFLayout("false")) d_ff_5 (
    .clk(IRE), .D(1'b1), .Q(d_ff_5_q), .preset(1'b0), .en(1'b1), .reset(INTR5));  // open: Qn
  D_Flip_Flop #(.trigger("rising"), .Pre_Clr_Positions("LEGACY"), .NegatePresetClear("false"), .enable("true"), .NewFFLayout("false")) d_ff_6 (
    .clk(IRF), .D(1'b1), .Q(d_ff_6_q), .preset(1'b0), .en(1'b1), .reset(INTR6));  // open: Qn
  Register #(.width(3), .trigger("rising"), .Select("low")) register_1 (
    .D(priority_encoder_1_out), .en(INTR), .Q(register_1_q), .clk(CLK_t), .clr(RST), .cs(1'b0), .preset(1'b0));
  or or_7 (or_7_out, d_ff_1_q, INTR1);
  and and_1 (and_1_out, or_7_out, ~CLR1);  // AND_Gate
  or or_8 (or_8_out, d_ff_2_q, INTR2);
  and and_2 (and_2_out, or_8_out, ~CLR2);  // AND_Gate
  or or_9 (or_9_out, d_ff_3_q, INTR3);
  and and_3 (and_3_out, or_9_out, ~CLR3);  // AND_Gate
  or or_10 (or_10_out, d_ff_4_q, INTR4);
  and and_4 (and_4_out, or_10_out, ~CLR4);  // AND_Gate
  or or_11 (or_11_out, d_ff_5_q, INTR5);
  and and_5 (and_5_out, or_11_out, ~CLR5);  // AND_Gate
  or or_12 (or_12_out, d_ff_6_q, INTR6);
  or or_13 (IRHAVE, INTR1, INTR2, INTR3, INTR4, INTR5, INTR6);
  or or_14 (or_14_out, ~IRHAVE, uret);  // OR_Gate
  Demultiplexer #(.select(3), .width(1), .tristate("false"), .disabled(0), .enable("false")) demultiplexer_1 (
    .out1(CLR1), .out2(CLR2), .out3(CLR3), .out4(CLR4), .out5(CLR5), .out6(CLR6), .in(uret),
    .sel(register_1_q));  // open: out0, out7
  D_Flip_Flop #(.trigger("rising"), .Pre_Clr_Positions("LEGACY"), .NegatePresetClear("false"), .enable("true"), .NewFFLayout("false")) IR1 (
    .clk(CLK_t), .D(and_1_out), .Q(INTR1), .preset(1'b0), .en(1'b1), .reset(1'b0));  // open: Qn
  D_Flip_Flop #(.trigger("rising"), .Pre_Clr_Positions("LEGACY"), .NegatePresetClear("false"), .enable("true"), .NewFFLayout("false")) IR2 (
    .clk(CLK_t), .D(and_2_out), .Q(INTR2), .preset(1'b0), .en(1'b1), .reset(1'b0));  // open: Qn
  D_Flip_Flop #(.trigger("rising"), .Pre_Clr_Positions("LEGACY"), .NegatePresetClear("false"), .enable("true"), .NewFFLayout("false")) IR3 (
    .clk(CLK_t), .D(and_3_out), .Q(INTR3), .preset(1'b0), .en(1'b1), .reset(1'b0));  // open: Qn
  D_Flip_Flop #(.trigger("rising"), .Pre_Clr_Positions("LEGACY"), .NegatePresetClear("false"), .enable("true"), .NewFFLayout("false")) IR4 (
    .clk(CLK_t), .D(and_4_out), .Q(INTR4), .preset(1'b0), .en(1'b1), .reset(1'b0));  // open: Qn
  D_Flip_Flop #(.trigger("rising"), .Pre_Clr_Positions("LEGACY"), .NegatePresetClear("false"), .enable("true"), .NewFFLayout("false")) IR5 (
    .clk(CLK_t), .D(and_5_out), .Q(INTR5), .preset(1'b0), .en(1'b1), .reset(1'b0));  // open: Qn
  and and_6 (and_6_out, or_12_out, ~CLR6);  // AND_Gate
  D_Flip_Flop #(.trigger("rising"), .Pre_Clr_Positions("LEGACY"), .NegatePresetClear("false"), .enable("true"), .NewFFLayout("true")) d_ff_7 (
    .clk(CLK_t), .D(or_14_out), .Q(IE), .preset(1'b0), .en(1'b1), .reset(1'b0));  // open: Qn
  D_Flip_Flop #(.trigger("rising"), .Pre_Clr_Positions("LEGACY"), .NegatePresetClear("false"), .enable("true"), .NewFFLayout("false")) IR6 (
    .clk(CLK_t), .D(and_6_out), .Q(INTR6), .preset(1'b0), .en(1'b1), .reset(1'b0));  // open: Qn
  and and_7 (INTR, IRHAVE, IE);
  Multiplexer #(.select(2), .width(32), .disabled(0), .enable("false")) multiplexer_2 (
    .in0(multiplexer_11_out), .in1(IR_PC), .in2(MEPC), .in3(multiplexer_11_out), .out(multiplexer_2_out),
    .sel(priority_encoder_2_out));
  Clock #(.highDuration(1), .lowDuration(1)) clock_1 (.out(CLK_t));
  Register #(.width(32), .trigger("rising"), .Select("low")) u_PC (
    .D(multiplexer_2_out), .en(or_15_out), .Q(PC), .clk(CLK_t), .clr(RST), .cs(1'b0), .preset(1'b0));
  or or_15 (or_15_out, GO, not_1_out);
  not not_1 (not_1_out, halt);
  Priority_Encoder #(.select(2), .disabled("Z")) priority_encoder_2 (
    .in0(1'b1), .in1(INTR), .in2(uret), .in3(1'b0), .out(priority_encoder_2_out), .en_in(1'b1));  // open: gs, en_out
  Register #(.width(32), .trigger("rising"), .Select("low")) register_2 (
    .D(multiplexer_11_out), .en(INTR), .Q(MEPC), .clk(CLK_t), .clr(RST), .cs(1'b0), .preset(1'b0));
  // RiscV_Probe riscv_probe_1: pin names not known; wires that end beside it: 1'b1, IR, IR[14:12], IR, IR[25], IR[30]
  ROM #(.addrWidth(10), .dataWidth(32), .Select("low")) IRPLACE (.addr(PC[11:2]), .data(IR));
  or or_16 (J, jal, jalr);
  Hex_Digit_Display hex_digit_display_1 (.value(LEDDATA[31:28]), .dp(1'b0));
  Hex_Digit_Display hex_digit_display_2 (.value(LEDDATA[27:24]), .dp(1'b0));
  // Probe on TOTALTIME
  assign bit_extender_1_out = {{12{1'b0}}, IR[31:12]};  // Bit_Extender bit_extender_1
  Hex_Digit_Display hex_digit_display_3 (.value(LEDDATA[23:20]), .dp(1'b0));
  Shifter #(.width(32), .shift("ll")) shifter_1 (.in(bit_extender_1_out), .\dist (5'b01100), .out(luidata));
  Hex_Digit_Display hex_digit_display_4 (.value(LEDDATA[19:16]), .dp(1'b0));
  CONTROLLER controller_1 (
    .OP(IR[6:2]), .Funct({IR[30], IR[25], IR[14:12]}), .IR21(IR[21]), .ALU_OP(controller_1_alu_op),
    .uret(uret), .MemToReg(controller_1_memtoreg), .ecall(ecall), .MemWrite(MemWrite),
    .ALU_SRC(controller_1_alu_src), .RegWrite(RegWrite), .S_type(controller_1_s_type),
    .Beq(controller_1_beq), .Bne(controller_1_bne), .Jalr(jalr), .JAL(jal), .half(half));  // open: CSR
  Multiplexer #(.select(1), .width(5), .disabled(0), .enable("false")) multiplexer_3 (
    .in0(IR[19:15]), .in1(5'b10001), .out(multiplexer_3_out), .sel(ecall));
  Multiplexer #(.select(1), .width(12), .disabled(0), .enable("false")) multiplexer_4 (
    .in0(IR[31:20]), .in1({IR[31:25], IR[11:7]}), .out(multiplexer_4_out), .sel(controller_1_s_type));
  Hex_Digit_Display hex_digit_display_5 (.value(LEDDATA[15:12]), .dp(1'b0));
  or or_17 (or_17_out, lui, RegWrite);
  Multiplexer #(.select(1), .width(5), .disabled(0), .enable("false")) multiplexer_5 (
    .in0(IR[24:20]), .in1(5'b01010), .out(multiplexer_5_out), .sel(ecall));
  Shifter #(.width(32), .shift("lr")) shifter_2 (.in(result), .\dist (5'b10000), .out(shifter_2_out));
  assign bit_extender_2_out = {{20{IR[31]}}, {IR[31], IR[7], IR[30:25], IR[11:8]}};  // Bit_Extender bit_extender_2
  assign bit_extender_3_out = {{12{IR[31]}}, {IR[31], IR[19:12], IR[20], IR[30:21]}};  // Bit_Extender bit_extender_3
  Hex_Digit_Display hex_digit_display_6 (.value(LEDDATA[11:8]), .dp(1'b0));
  Comparator #(.width(5), .mode("twosComplement")) comparator_1 (.a(IR[6:2]), .b(5'b01101), .eq(lui));  // open: gt, lt
  REGIFILE regifile_1 (
    .Din(RDin), .Clk(CLK_t), .R1(regifile_1_r1), .R2(MDin), .WE(or_17_out), .WAdr(IR[11:7]),
    .R1Adr(multiplexer_3_out), .R2Adr(multiplexer_5_out));
  Shifter #(.width(32), .shift("ll")) shifter_3 (.in(bit_extender_2_out), .\dist (5'b00001), .out(shifter_3_out));
  Shifter #(.width(32), .shift("ll")) shifter_4 (.in(bit_extender_3_out), .\dist (5'b00001), .out(shifter_4_out));
  Hex_Digit_Display hex_digit_display_7 (.value(LEDDATA[7:4]), .dp(1'b0));
  not not_2 (not_2_out, RegWrite);
  assign bit_extender_4_out = {{20{multiplexer_4_out[11]}}, multiplexer_4_out};  // Bit_Extender bit_extender_4
  Multiplexer #(.select(1), .width(32), .disabled(0), .enable("false")) multiplexer_6 (
    .in0(result), .in1(shifter_2_out), .out(multiplexer_6_out), .sel(aluresult[1]));
  Adder #(.width(32)) adder_1 (.a(PC), .b(32'h4), .out(adder_1_out), .cin(1'b0));  // open: cout
  Adder #(.width(32)) adder_2 (.a(shifter_3_out), .b(PC), .out(adder_2_out), .cin(1'b0));  // open: cout
  Adder #(.width(32)) adder_3 (.a(shifter_4_out), .b(PC), .out(adder_3_out), .cin(1'b0));  // open: cout
  assign and_8_out = {aluresult[31:12], ADDR, aluresult[1:0]} & 32'hfffffffe;  // AND_Gate and_8, 32 bits wide
  Hex_Digit_Display hex_digit_display_8 (.value(LEDDATA[3:0]), .dp(1'b0));
  Comparator #(.width(32), .mode("twosComplement")) comparator_2 (
    .a(32'h22), .b(regifile_1_r1), .eq(comparator_2_eq));  // open: gt, lt
  Multiplexer #(.select(1), .width(32), .disabled(0), .enable("false")) multiplexer_7 (
    .in0(MDin), .in1(bit_extender_4_out), .out(multiplexer_7_out), .sel(controller_1_alu_src));
  assign and_9_out = multiplexer_6_out & 32'hffff;  // AND_Gate and_9, 32 bits wide
  not not_3 (not_3_out, alu_1_equal);
  and and_10 (and_10_out, not_2_out, alu_1_less);
  ALU alu_1 (
    .X(regifile_1_r1), .Y(multiplexer_7_out), .AluOP(controller_1_alu_op), .Equal(alu_1_equal),
    .LESS(alu_1_less), .Result({aluresult[31:12], ADDR, aluresult[1:0]}));  // open: NOTLESS, Result_2
  Multiplexer #(.select(1), .width(32), .disabled(0), .enable("false")) multiplexer_8 (
    .in0(result), .in1(and_9_out), .out(multiplexer_8_out), .sel(half));
  Priority_Encoder #(.select(2), .disabled(0)) priority_encoder_3 (
    .in0(1'b1), .in1(B), .in2(jal), .in3(jalr), .out(priority_encoder_3_out), .en_in(1'b1));  // open: gs, en_out
  and and_11 (and_11_out, alu_1_equal, controller_1_beq);
  and and_12 (and_12_out, not_3_out, controller_1_bne);
  Multiplexer #(.select(1), .width(32), .disabled(0), .enable("false")) multiplexer_9 (
    .in0(multiplexer_8_out), .in1(adder_1_out), .out(multiplexer_9_out), .sel(J));
  Multiplexer #(.select(1), .width(32), .disabled("Z"), .enable("false")) multiplexer_10 (
    .in0(multiplexer_9_out), .in1(luidata), .out(RDin), .sel(lui));
  Multiplexer #(.select(2), .width(32), .disabled(0), .enable("false")) multiplexer_11 (
    .in0(adder_1_out), .in1(adder_2_out), .in2(adder_3_out), .in3(and_8_out), .out(multiplexer_11_out),
    .sel(priority_encoder_3_out));
  or or_18 (or_18_out, and_11_out, and_12_out);
  and and_13 (led, ecall, comparator_2_eq);
  or or_19 (B, or_18_out, and_10_out);
  not not_4 (not_4_out, MemWrite);
  Multiplexer #(.select(1), .width(32), .disabled(0), .enable("false")) multiplexer_12 (
    .in0({32{1'b0}}), .in1(MDin), .out(multiplexer_12_out), .sel(led));
  not not_5 (not_5_out, comparator_2_eq);
  RAM #(.addrWidth(10), .dataWidth(32), .bus("separate"), .Select("high")) DATAPLACE (
    .addr(ADDR), .din(MDin), .data(DATAPLACE_data), .str(MemWrite), .sel(1'b1), .clk(CLK_t), .ld(not_4_out),
    .clr(1'b0));
  Register #(.width(32), .trigger("rising"), .Select("low")) register_3 (
    .D(multiplexer_12_out), .en(led), .Q(LEDDATA), .clk(CLK_t), .clr(RST), .cs(1'b0), .preset(1'b0));
  or or_20 (or_20_out, GO, not_6_out);
  not not_6 (not_6_out, halt);
  and and_14 (halt, ecall, not_5_out);
  Multiplexer #(.select(1), .width(32), .disabled(0), .enable("false")) multiplexer_13 (
    .in0({aluresult[31:12], ADDR, aluresult[1:0]}), .in1(DATAPLACE_data), .out(result),
    .sel(controller_1_memtoreg));
  Counter #(.width(16), .max('hffff), .ongoal("wrap"), .trigger("rising"), .behavior("new")) counter_1 (
    .load(1'b0), .D({16{1'b0}}), .count(or_20_out), .Q(TOTALTIME), .clk(CLK_t), .clr(RST), .preset(1'b0),
    .down(1'b0));  // open: carry
  and and_15 (and_15_out, MemWrite, comparator_3_gt);
  Comparator #(.width(10), .mode("unsigned")) comparator_3 (
    .a(10'h20), .b(ADDR), .gt(comparator_3_gt));  // open: eq, lt
  MAZEMAP mazemap_1 (
    .WE(and_15_out), .R1(mazemap_1_r1), .R9(mazemap_1_r9), .R17(mazemap_1_r17), .R25(mazemap_1_r25),
    .R2(mazemap_1_r2), .R10(mazemap_1_r10), .R18(mazemap_1_r18), .R26(mazemap_1_r26), .R3(mazemap_1_r3),
    .R11(mazemap_1_r11), .R19(mazemap_1_r19), .R27(mazemap_1_r27), .R4(mazemap_1_r4), .R12(mazemap_1_r12),
    .R20(mazemap_1_r20), .R28(mazemap_1_r28), .R5(mazemap_1_r5), .R13(mazemap_1_r13), .R21(mazemap_1_r21),
    .R29(mazemap_1_r29), .R6(mazemap_1_r6), .R14(mazemap_1_r14), .R22(mazemap_1_r22), .R30(mazemap_1_r30),
    .Addr(ADDR), .R7(mazemap_1_r7), .R15(mazemap_1_r15), .R23(mazemap_1_r23), .R31(mazemap_1_r31),
    .R8(mazemap_1_r8), .R16(mazemap_1_r16), .R24(mazemap_1_r24), .R32(mazemap_1_r32), .CLK(CLK_t), .RST(RST),
    .Data(MDin));
  DISPLAY display_1 (
    .WE(led), .A1(mazemap_1_r1), .R1(R1), .A2(mazemap_1_r2), .R2(R2), .A3(mazemap_1_r3), .R3(R3),
    .A4(mazemap_1_r4), .R4(R4), .A5(mazemap_1_r5), .R5(R5), .A6(mazemap_1_r6), .R6(R6), .A7(mazemap_1_r7),
    .R7(R7), .A8(mazemap_1_r8), .R8(R8), .A9(mazemap_1_r9), .R9(R9), .A10(mazemap_1_r10), .R10(R10),
    .A11(mazemap_1_r11), .R11(R11), .A12(mazemap_1_r12), .R12(R12), .A13(mazemap_1_r13), ._13(R13),
    .A14(mazemap_1_r14), .R14(R14), .A15(mazemap_1_r15), .R15(R15), .A16(mazemap_1_r16), .R16(R16),
    .A17(mazemap_1_r17), .R17(R17), .A18(mazemap_1_r18), .R18(R18), .A19(mazemap_1_r19), .R19(R19),
    .A20(mazemap_1_r20), .R20(R20), .A21(mazemap_1_r21), .R21(R21), .A22(mazemap_1_r22), .R22(R22),
    .A23(mazemap_1_r23), .R23(R23), .A24(mazemap_1_r24), .R24(R24), .A25(mazemap_1_r25), .R25(R25),
    .A26(mazemap_1_r26), .R26(R26), .A27(mazemap_1_r27), .R27(R27), .A28(mazemap_1_r28), .R28(R28),
    .A29(mazemap_1_r29), .R29(R29), .A30(mazemap_1_r30), .R30(R30), .A31(mazemap_1_r31), .R31(R31),
    .A32(mazemap_1_r32), .R32(R32), .CLK(CLK_t), .RST(RST));

  // Other names for the same wires on the sheet: high = aluresult[1]; aluresult[11:2] = ADDR

  // Notes on the sheet:
  //   保存断点
  //   contents of IRPLACE (hex, n*v repeats v):
  //   4b00006f 18091863 10080337 130313 602023 10080337 30313 602223 1f088337 e3f30313 602423 1080337
  //   20030313 602623 e1080337 20030313 602823 1008337 ff830313 602a23 1004337 30313 602c23 ff004337 30313
  //   602e23 100fd337 ff830313 2602023 10081337 80030313 2602223 10081337 80030313 2602423 13f81337
  //   80030313 2602623 120c0337 8ff30313 2602823 120a0337 8030313 2602a23 123a0337 8030313 2602c23
  //   10220337 8030313 2602e23 10230337 f0030313 4602023 11e20337 830313 4602223 11000337 830313 4602423
  //   11000337 830313 4602623 ff3ff337 7f830313 4602823 1201337 80030313 4602a23 1201337 80030313 4602c23
  //   1201337 80030313 4602e23 f92e0337 3ff30313 6602023 41081337 80030313 6602223 41081337 80030313
  //   6602423 41081337 80030313 6602623 1ff84337 f0830313 6602823 2337 830313 6602a23 2337 830313 6602c23
  //   1fff0337 830313 6602e23 2200893 73 100913 200073 18091863 16e10337 ff930313 602023 10041337 e0830313
  //   602223 10072337 4230313 602423 10fc4337 ff830313 602623 125337 9230313 602823 ff149337 aa30313
  //   602a23 5a5337 c630313 602c23 ffd47337 49f30313 602e23 8104337 4aa30313 2602023 5a18a337 6d530313
  //   2602223 a5140337 4aa30313 2602423 60000337 cff30313 2602623 1088b337 a930313 2602823 14551337
  //   8830313 2602a23 f4224337 74a30313 2602c23 5ff6337 42a30313 2602e23 ff844337 50a30313 4602023
  //   11476337 d4930313 4602223 49205337 24d30313 4602423 ff1fd337 14b30313 4602623 20502337 fd930313
  //   4602823 10956337 89930313 4602a23 c9143337 52d30313 4602c23 1ff3f337 20930313 4602e23 80132337
  //   5ff30313 6602023 80868337 48430313 6602223 9ffe5337 4c430313 6602423 403337 5c730313 6602623
  //   30445337 29230313 6602823 fc7e9337 5fd30313 6602a23 4c122337 88a30313 6602c23 d337 4830313 6602e23
  //   2200893 73 100913 200073 4090a63 1f00313 16640863 100313 6403b3 731e33 249e93 eaf03 1cf7fb3 140f9a63
  //   640433 1cf6f33 1e5e13 1cf4f33 1eea023 2200893 73 1f00393 740463 200073 20748863 200073 4090a63 393
  //   10740c63 100313 406403b3 731e33 249e93 eaf03 1cf7fb3 e0f9e63 40640433 1cf6f33 1e1e13 1cf4f33 1eea023
  //   2200893 73 1f00393 740463 200073 1a748c63 200073 6090063 1f00393 c748063 100313 831e33 6483b3 239e93
  //   eaf03 1cf7fb3 a0f9263 6484b3 1cf6f33 1eea023 400393 407e8eb3 eaf03 1cf4f33 1eea023 2200893 73
  //   1f00393 740463 200073 14748a63 200073 393 4790e63 393 4748c63 100313 831e33 406483b3 239e93 eaf03
  //   1cf7fb3 20f9e63 406484b3 1cf6f33 1eea023 4e8e93 eaf03 1cf4f33 1eea023 2200893 73 1f00393 740463
  //   200073 e748863 200073 6400513 73 200073 413 493 11088337 cf830313 602c23 1b141337 88030313 602e23
  //   153e1337 f830313 2602023 11222337 8030313 2602223 11228337 cf830313 2602423 60e5337 ea030313 2602a23
  //   208b337 8a030313 2602c23 20ef337 e4030313 2602e23 208a337 24030313 4602023 74eb337 e4030313 4602223
  //   70a5337 ec030313 4602823 10ab337 aa030313 4602a23 70ef337 ea030313 4602c23 40ab337 ca030313 4602e23
  //   74ab337 ac030313 6602023 2200893 73 5*13 fedff06f 100993 313 602023 313 602223 313 602423 313 602623
  //   313 602823 313 602a23 313 602c23 313 602e23 313 2602023 313 2602223 313 2602423 313 2602623 313
  //   2602823 75777337 77230313 2602a23 45445337 44230313 2602c23 75447337 77230313 2602e23 15444337
  //   11030313 4602023 77777337 77230313 4602223 313 4602423 313 4602623 313 4602823 313 4602a23 313
  //   4602c23 313 4602e23 313 6602023 313 6602223 313 6602423 313 6602623 313 6602823 313 6602a23 313
  //   6602c23 313 6602e23 2200893 73 ec9ff06f
  //   JAL
  //   JALR
  //   URET
  //   Beq
  //   Bne
  //   MemToReg
  //   MemWrite
  //   AluOP
  //   AluSrcB
  //   RegWrite
  //   half
  //   PC+4
  //   BEQ/BNE
  //   JAL
  //   JALR
endmodule

module CONTROLLER (
  input  [4:0] OP,
  input  [4:0] Funct,
  input  IR21,
  output [3:0] ALU_OP,
  output uret,
  output MemToReg,
  output ecall,
  output MemWrite,
  output ALU_SRC,
  output RegWrite,
  output S_type,
  output Beq,
  output Bne,
  output Jalr,
  output JAL,
  output half,
  output CSR
);

  wire controlsignal_1_ecall;

  COMPUTESIGNAL computesignal_1 (
    .OP2(OP[0]), .OP3(OP[1]), .OP4(OP[2]), .OP5(OP[3]), .OP6(OP[4]), .F12(Funct[0]), .F13(Funct[1]),
    .F14(Funct[2]), .F25(Funct[3]), .F30(Funct[4]), .S0(ALU_OP[0]), .S1(ALU_OP[1]), .S2(ALU_OP[2]),
    .S3(ALU_OP[3]));
  CONTROLSIGNAL controlsignal_1 (
    .OP2(OP[0]), .OP3(OP[1]), .OP4(OP[2]), .OP5(OP[3]), .OP6(OP[4]), .F12(Funct[0]), .F13(Funct[1]),
    .F14(Funct[2]), .F25(Funct[3]), .F30(Funct[4]), .MemToReg(MemToReg), .MemWrite(MemWrite),
    .ALU_SRC(ALU_SRC), .RegWrite(RegWrite), .ecall(controlsignal_1_ecall), .S_Type(S_type), .BEQ(Beq),
    .BNE(Bne), .JALR(Jalr), .JAL(JAL), .half(half), .CSR(CSR));
  and and_1 (uret, IR21, controlsignal_1_ecall);
  and and_2 (ecall, ~IR21, controlsignal_1_ecall);  // AND_Gate

  // Other names for the same wires on the sheet: OP_CODE[4:0] = OP
endmodule

module COMPUTESIGNAL (
  input  OP2,
  input  OP3,
  input  OP4,
  input  OP5,
  input  OP6,
  input  F12,
  input  F13,
  input  F14,
  input  F25,
  input  F30,
  output S0,
  output S1,
  output S2,
  output S3
);

  wire and_1_out, and_2_out, and_3_out, and_4_out, and_5_out, and_6_out, and_7_out, and_8_out, and_9_out,
       and_10_out, and_11_out, and_12_out, and_13_out, and_14_out, and_15_out, and_16_out, and_17_out,
       and_18_out, and_19_out, and_20_out, and_21_out, and_22_out, and_23_out, and_24_out, and_25_out,
       and_26_out, and_27_out, and_28_out, and_29_out, and_30_out, and_31_out, and_32_out, and_33_out,
       and_34_out, and_35_out, and_36_out, and_37_out, and_38_out, and_39_out, and_40_out, and_41_out,
       and_42_out, and_43_out, not_1_out, not_2_out, not_3_out, not_4_out, not_5_out, not_6_out, not_7_out,
       not_8_out, not_9_out, not_10_out, not_11_out, not_12_out, not_13_out, not_14_out, not_15_out,
       not_16_out, not_17_out, not_18_out, not_19_out, not_20_out, not_21_out, not_22_out, not_23_out,
       not_24_out, not_25_out, not_26_out, not_27_out, not_28_out, not_29_out, not_30_out, not_31_out,
       not_32_out, not_33_out, not_34_out, not_35_out, not_36_out, not_37_out, not_38_out, not_39_out,
       not_40_out, not_41_out, not_42_out, not_43_out, not_44_out, not_45_out, not_46_out, not_47_out,
       not_48_out, not_49_out, not_50_out, not_51_out, not_52_out, not_53_out, not_54_out, not_55_out,
       not_56_out, not_57_out, not_58_out, not_59_out, not_60_out, not_61_out, not_62_out, not_63_out,
       not_64_out, not_65_out, not_66_out, not_67_out, not_68_out, not_69_out, not_70_out, not_71_out,
       not_72_out, not_73_out, not_74_out, not_75_out, not_76_out, not_77_out, not_78_out, not_79_out,
       not_80_out, not_81_out, not_82_out, not_83_out, not_84_out, not_85_out, not_86_out, not_87_out,
       not_88_out, not_89_out, not_90_out, not_91_out, not_92_out, not_93_out, not_94_out, not_95_out,
       not_96_out, not_97_out, not_98_out, not_99_out, not_100_out, not_101_out, not_102_out, not_103_out,
       not_104_out, not_105_out, not_106_out, not_107_out, not_108_out, not_109_out, not_110_out,
       not_111_out, not_112_out, not_113_out, not_114_out, not_115_out, not_116_out, not_117_out,
       not_118_out, not_119_out, not_120_out, not_121_out, not_122_out, not_123_out, not_124_out,
       not_125_out, not_126_out, not_127_out, not_128_out, not_129_out, not_130_out, not_131_out,
       not_132_out, not_133_out, not_134_out, not_135_out, not_136_out, not_137_out, not_138_out,
       not_139_out, not_140_out, not_141_out, not_142_out, not_143_out, not_144_out, not_145_out,
       not_146_out, not_147_out, not_148_out, not_149_out, not_150_out, not_151_out, not_152_out,
       not_153_out, not_154_out, not_155_out, not_156_out, not_157_out, not_158_out, not_159_out,
       not_160_out, not_161_out, not_162_out, not_163_out, not_164_out, not_165_out, not_166_out,
       not_167_out, not_168_out, not_169_out, not_170_out, not_171_out, not_172_out, not_173_out,
       not_174_out, not_175_out, not_176_out, not_177_out, not_178_out, not_179_out, not_180_out,
       not_181_out, not_182_out, not_183_out, not_184_out, not_185_out, not_186_out, not_187_out,
       not_188_out, not_189_out, not_190_out, not_191_out, not_192_out, not_193_out, not_194_out,
       not_195_out, not_196_out, not_197_out, not_198_out, not_199_out, not_200_out, not_201_out,
       not_202_out, not_203_out, not_204_out, not_205_out, not_206_out, not_207_out, not_208_out,
       not_209_out, not_210_out, not_211_out, not_212_out, not_213_out, not_214_out, not_215_out,
       not_216_out, not_217_out, not_218_out, not_219_out, not_220_out, not_221_out, not_222_out,
       not_223_out, not_224_out, not_225_out, not_226_out, not_227_out, not_228_out, not_229_out,
       not_230_out, not_231_out, not_232_out, not_233_out, not_234_out, not_235_out, not_236_out,
       not_237_out, not_238_out, not_239_out, not_240_out, not_241_out, not_242_out, not_243_out, not_244_out;

  not not_1 (not_1_out, F30);
  not not_2 (not_2_out, F25);
  not not_3 (not_3_out, F14);
  not not_4 (not_4_out, F13);
  not not_5 (not_5_out, F12);
  not not_6 (not_6_out, OP6);
  not not_7 (not_7_out, OP3);
  not not_8 (not_8_out, OP2);
  not not_9 (not_9_out, F30);
  not not_10 (not_10_out, F25);
  not not_11 (not_11_out, OP6);
  not not_12 (not_12_out, OP3);
  not not_13 (not_13_out, OP2);
  not not_14 (not_14_out, F30);
  not not_15 (not_15_out, F25);
  not not_16 (not_16_out, F14);
  not not_17 (not_17_out, F12);
  not not_18 (not_18_out, OP6);
  not not_19 (not_19_out, OP3);
  not not_20 (not_20_out, OP2);
  not not_21 (not_21_out, F14);
  not not_22 (not_22_out, F13);
  not not_23 (not_23_out, F12);
  not not_24 (not_24_out, OP6);
  not not_25 (not_25_out, OP5);
  not not_26 (not_26_out, OP3);
  not not_27 (not_27_out, OP2);
  not not_28 (not_28_out, OP6);
  not not_29 (not_29_out, OP5);
  not not_30 (not_30_out, OP3);
  not not_31 (not_31_out, OP2);
  not not_32 (not_32_out, F13);
  not not_33 (not_33_out, F12);
  not not_34 (not_34_out, OP6);
  not not_35 (not_35_out, OP5);
  not not_36 (not_36_out, OP3);
  not not_37 (not_37_out, OP2);
  not not_38 (not_38_out, F14);
  not not_39 (not_39_out, F12);
  not not_40 (not_40_out, OP6);
  not not_41 (not_41_out, OP5);
  not not_42 (not_42_out, OP3);
  not not_43 (not_43_out, OP2);
  not not_44 (not_44_out, F25);
  not not_45 (not_45_out, F13);
  not not_46 (not_46_out, OP6);
  not not_47 (not_47_out, OP5);
  not not_48 (not_48_out, OP3);
  not not_49 (not_49_out, OP2);
  not not_50 (not_50_out, F14);
  not not_51 (not_51_out, F12);
  not not_52 (not_52_out, OP6);
  not not_53 (not_53_out, OP5);
  not not_54 (not_54_out, OP4);
  not not_55 (not_55_out, OP3);
  not not_56 (not_56_out, OP2);
  not not_57 (not_57_out, F14);
  not not_58 (not_58_out, F12);
  not not_59 (not_59_out, OP6);
  not not_60 (not_60_out, OP4);
  not not_61 (not_61_out, OP3);
  not not_62 (not_62_out, OP2);
  not not_63 (not_63_out, F14);
  not not_64 (not_64_out, F13);
  not not_65 (not_65_out, F12);
  not not_66 (not_66_out, OP4);
  not not_67 (not_67_out, OP3);
  not not_68 (not_68_out, OP3);
  not not_69 (not_69_out, OP2);
  not not_70 (not_70_out, F30);
  not not_71 (not_71_out, F25);
  not not_72 (not_72_out, F13);
  not not_73 (not_73_out, F12);
  not not_74 (not_74_out, OP6);
  not not_75 (not_75_out, OP3);
  not not_76 (not_76_out, OP2);
  not not_77 (not_77_out, F13);
  not not_78 (not_78_out, OP6);
  not not_79 (not_79_out, OP5);
  not not_80 (not_80_out, OP4);
  not not_81 (not_81_out, OP3);
  not not_82 (not_82_out, OP2);
  not not_83 (not_83_out, F13);
  not not_84 (not_84_out, F12);
  not not_85 (not_85_out, OP4);
  not not_86 (not_86_out, OP3);
  not not_87 (not_87_out, OP2);
  not not_88 (not_88_out, F25);
  not not_89 (not_89_out, F14);
  not not_90 (not_90_out, F13);
  not not_91 (not_91_out, F12);
  not not_92 (not_92_out, OP6);
  not not_93 (not_93_out, OP3);
  not not_94 (not_94_out, OP2);
  not not_95 (not_95_out, F30);
  not not_96 (not_96_out, F25);
  not not_97 (not_97_out, OP6);
  not not_98 (not_98_out, OP3);
  not not_99 (not_99_out, OP2);
  not not_100 (not_100_out, F30);
  not not_101 (not_101_out, F25);
  not not_102 (not_102_out, F14);
  not not_103 (not_103_out, F12);
  not not_104 (not_104_out, OP6);
  not not_105 (not_105_out, OP3);
  not not_106 (not_106_out, OP2);
  not not_107 (not_107_out, OP6);
  not not_108 (not_108_out, OP5);
  not not_109 (not_109_out, OP3);
  not not_110 (not_110_out, OP2);
  not not_111 (not_111_out, F14);
  not not_112 (not_112_out, F12);
  not not_113 (not_113_out, OP6);
  not not_114 (not_114_out, OP5);
  not not_115 (not_115_out, OP3);
  not not_116 (not_116_out, OP2);
  not not_117 (not_117_out, F30);
  not not_118 (not_118_out, F25);
  not not_119 (not_119_out, F13);
  not not_120 (not_120_out, OP6);
  not not_121 (not_121_out, OP5);
  not not_122 (not_122_out, OP3);
  not not_123 (not_123_out, OP2);
  not not_124 (not_124_out, OP3);
  not not_125 (not_125_out, OP2);
  not not_126 (not_126_out, F13);
  not not_127 (not_127_out, F12);
  not not_128 (not_128_out, OP4);
  not not_129 (not_129_out, OP3);
  not not_130 (not_130_out, OP2);
  not not_131 (not_131_out, F30);
  not not_132 (not_132_out, F25);
  not not_133 (not_133_out, F14);
  not not_134 (not_134_out, F13);
  not not_135 (not_135_out, F12);
  not not_136 (not_136_out, OP6);
  not not_137 (not_137_out, OP3);
  not not_138 (not_138_out, OP2);
  not not_139 (not_139_out, F25);
  not not_140 (not_140_out, F14);
  not not_141 (not_141_out, F13);
  not not_142 (not_142_out, F12);
  not not_143 (not_143_out, OP6);
  not not_144 (not_144_out, OP3);
  not not_145 (not_145_out, OP2);
  not not_146 (not_146_out, F30);
  not not_147 (not_147_out, F25);
  not not_148 (not_148_out, OP6);
  not not_149 (not_149_out, OP3);
  not not_150 (not_150_out, OP2);
  not not_151 (not_151_out, F30);
  not not_152 (not_152_out, F25);
  not not_153 (not_153_out, F14);
  not not_154 (not_154_out, OP6);
  not not_155 (not_155_out, OP3);
  not not_156 (not_156_out, OP2);
  not not_157 (not_157_out, F14);
  not not_158 (not_158_out, F13);
  not not_159 (not_159_out, F12);
  not not_160 (not_160_out, OP6);
  not not_161 (not_161_out, OP5);
  not not_162 (not_162_out, OP3);
  not not_163 (not_163_out, OP2);
  not not_164 (not_164_out, OP6);
  not not_165 (not_165_out, OP5);
  not not_166 (not_166_out, OP3);
  not not_167 (not_167_out, OP2);
  not not_168 (not_168_out, F14);
  not not_169 (not_169_out, F12);
  not not_170 (not_170_out, OP6);
  not not_171 (not_171_out, OP5);
  not not_172 (not_172_out, OP4);
  not not_173 (not_173_out, OP3);
  not not_174 (not_174_out, OP2);
  not not_175 (not_175_out, F14);
  not not_176 (not_176_out, F12);
  not not_177 (not_177_out, OP6);
  not not_178 (not_178_out, OP4);
  not not_179 (not_179_out, OP3);
  not not_180 (not_180_out, OP2);
  not not_181 (not_181_out, F14);
  not not_182 (not_182_out, F13);
  not not_183 (not_183_out, F12);
  not not_184 (not_184_out, OP4);
  not not_185 (not_185_out, OP3);
  not not_186 (not_186_out, OP3);
  not not_187 (not_187_out, OP2);
  not not_188 (not_188_out, F13);
  not not_189 (not_189_out, OP6);
  not not_190 (not_190_out, OP5);
  not not_191 (not_191_out, OP4);
  not not_192 (not_192_out, OP3);
  not not_193 (not_193_out, OP2);
  not not_194 (not_194_out, F30);
  not not_195 (not_195_out, F25);
  not not_196 (not_196_out, F12);
  not not_197 (not_197_out, OP6);
  not not_198 (not_198_out, OP3);
  not not_199 (not_199_out, OP2);
  not not_200 (not_200_out, F30);
  not not_201 (not_201_out, F25);
  not not_202 (not_202_out, F14);
  not not_203 (not_203_out, F12);
  not not_204 (not_204_out, OP6);
  not not_205 (not_205_out, OP3);
  not not_206 (not_206_out, OP2);
  not not_207 (not_207_out, F30);
  not not_208 (not_208_out, F25);
  not not_209 (not_209_out, F14);
  not not_210 (not_210_out, OP6);
  not not_211 (not_211_out, OP3);
  not not_212 (not_212_out, OP2);
  not not_213 (not_213_out, F12);
  not not_214 (not_214_out, OP6);
  not not_215 (not_215_out, OP5);
  not not_216 (not_216_out, OP3);
  not not_217 (not_217_out, OP2);
  not not_218 (not_218_out, F13);
  not not_219 (not_219_out, F12);
  not not_220 (not_220_out, OP6);
  not not_221 (not_221_out, OP5);
  not not_222 (not_222_out, OP3);
  not not_223 (not_223_out, OP2);
  not not_224 (not_224_out, F14);
  not not_225 (not_225_out, F12);
  not not_226 (not_226_out, OP6);
  not not_227 (not_227_out, OP5);
  not not_228 (not_228_out, OP3);
  not not_229 (not_229_out, OP2);
  not not_230 (not_230_out, F12);
  not not_231 (not_231_out, OP3);
  not not_232 (not_232_out, OP2);
  not not_233 (not_233_out, F30);
  not not_234 (not_234_out, F25);
  not not_235 (not_235_out, F13);
  not not_236 (not_236_out, F12);
  not not_237 (not_237_out, OP6);
  not not_238 (not_238_out, OP3);
  not not_239 (not_239_out, OP2);
  not not_240 (not_240_out, F13);
  not not_241 (not_241_out, F12);
  not not_242 (not_242_out, OP4);
  not not_243 (not_243_out, OP3);
  not not_244 (not_244_out, OP2);
  and and_1 (and_1_out, not_1_out, not_2_out, not_3_out, not_4_out, not_5_out, not_6_out, OP5, OP4, not_7_out, not_8_out);
  and and_2 (and_2_out, not_9_out, not_10_out, F14, F13, F12, not_11_out, OP5, OP4, not_12_out, not_13_out);
  and and_3 (and_3_out, not_14_out, not_15_out, not_16_out, F13, not_17_out, not_18_out, OP5, OP4, not_19_out, not_20_out);
  and and_4 (and_4_out, not_21_out, not_22_out, not_23_out, not_24_out, not_25_out, OP4, not_26_out, not_27_out);
  and and_5 (and_5_out, F14, F13, F12, not_28_out, not_29_out, OP4, not_30_out, not_31_out);
  and and_6 (and_6_out, F14, not_32_out, not_33_out, not_34_out, not_35_out, OP4, not_36_out, not_37_out);
  and and_7 (and_7_out, not_38_out, F13, not_39_out, not_40_out, not_41_out, OP4, not_42_out, not_43_out);
  and and_8 (and_8_out, F30, not_44_out, F14, not_45_out, F12, not_46_out, not_47_out, OP4, not_48_out, not_49_out);
  and and_9 (and_9_out, not_50_out, F13, not_51_out, not_52_out, not_53_out, not_54_out, not_55_out, not_56_out);
  and and_10 (and_10_out, not_57_out, F13, not_58_out, not_59_out, OP5, not_60_out, not_61_out, not_62_out);
  and and_11 (and_11_out, not_63_out, not_64_out, not_65_out, OP6, OP5, not_66_out, not_67_out, OP2);
  and and_12 (and_12_out, F14, F13, F12, OP6, OP5, OP4, not_68_out, not_69_out);
  and and_13 (and_13_out, not_70_out, not_71_out, F14, not_72_out, not_73_out, not_74_out, OP5, OP4, not_75_out, not_76_out);
  and and_14 (and_14_out, F14, not_77_out, F12, not_78_out, not_79_out, not_80_out, not_81_out, not_82_out);
  and and_15 (and_15_out, F14, not_83_out, not_84_out, OP6, OP5, not_85_out, not_86_out, not_87_out);
  and and_16 (and_16_out, F30, not_88_out, not_89_out, not_90_out, not_91_out, not_92_out, OP5, OP4, not_93_out, not_94_out);
  and and_17 (and_17_out, not_95_out, not_96_out, F14, F13, F12, not_97_out, OP5, OP4, not_98_out, not_99_out);
  and and_18 (and_18_out, not_100_out, not_101_out, not_102_out, F13, not_103_out, not_104_out, OP5, OP4, not_105_out, not_106_out);
  and and_19 (and_19_out, F14, F13, F12, not_107_out, not_108_out, OP4, not_109_out, not_110_out);
  and and_20 (and_20_out, not_111_out, F13, not_112_out, not_113_out, not_114_out, OP4, not_115_out, not_116_out);
  and and_21 (and_21_out, not_117_out, not_118_out, F14, not_119_out, F12, not_120_out, not_121_out, OP4, not_122_out, not_123_out);
  and and_22 (and_22_out, F14, F13, F12, OP6, OP5, OP4, not_124_out, not_125_out);
  and and_23 (and_23_out, F14, not_126_out, not_127_out, OP6, OP5, not_128_out, not_129_out, not_130_out);
  and and_24 (and_24_out, not_131_out, not_132_out, not_133_out, not_134_out, not_135_out, not_136_out, OP5, OP4, not_137_out, not_138_out);
  and and_25 (and_25_out, F30, not_139_out, not_140_out, not_141_out, not_142_out, not_143_out, OP5, OP4, not_144_out, not_145_out);
  and and_26 (and_26_out, not_146_out, not_147_out, F14, F13, F12, not_148_out, OP5, OP4, not_149_out, not_150_out);
  and and_27 (and_27_out, not_151_out, not_152_out, not_153_out, F13, F12, not_154_out, OP5, OP4, not_155_out, not_156_out);
  and and_28 (and_28_out, not_157_out, not_158_out, not_159_out, not_160_out, not_161_out, OP4, not_162_out, not_163_out);
  and and_29 (and_29_out, F14, F13, F12, not_164_out, not_165_out, OP4, not_166_out, not_167_out);
  and and_30 (and_30_out, not_168_out, F13, not_169_out, not_170_out, not_171_out, not_172_out, not_173_out, not_174_out);
  and and_31 (and_31_out, not_175_out, F13, not_176_out, not_177_out, OP5, not_178_out, not_179_out, not_180_out);
  and and_32 (and_32_out, not_181_out, not_182_out, not_183_out, OP6, OP5, not_184_out, not_185_out, OP2);
  and and_33 (and_33_out, F14, F13, F12, OP6, OP5, OP4, not_186_out, not_187_out);
  and and_34 (and_34_out, F14, not_188_out, F12, not_189_out, not_190_out, not_191_out, not_192_out, not_193_out);
  and and_35 (and_35_out, not_194_out, not_195_out, F14, F13, not_196_out, not_197_out, OP5, OP4, not_198_out, not_199_out);
  and and_36 (and_36_out, not_200_out, not_201_out, not_202_out, F13, not_203_out, not_204_out, OP5, OP4, not_205_out, not_206_out);
  and and_37 (and_37_out, not_207_out, not_208_out, not_209_out, F13, F12, not_210_out, OP5, OP4, not_211_out, not_212_out);
  and and_38 (and_38_out, F14, F13, not_213_out, not_214_out, not_215_out, OP4, not_216_out, not_217_out);
  and and_39 (and_39_out, F14, not_218_out, not_219_out, not_220_out, not_221_out, OP4, not_222_out, not_223_out);
  and and_40 (and_40_out, not_224_out, F13, not_225_out, not_226_out, not_227_out, OP4, not_228_out, not_229_out);
  and and_41 (and_41_out, F14, F13, not_230_out, OP6, OP5, OP4, not_231_out, not_232_out);
  and and_42 (and_42_out, not_233_out, not_234_out, F14, not_235_out, not_236_out, not_237_out, OP5, OP4, not_238_out, not_239_out);
  and and_43 (and_43_out, F14, not_240_out, not_241_out, OP6, OP5, not_242_out, not_243_out, not_244_out);
  or or_1 (S0, and_1_out, and_2_out, and_3_out, and_4_out, and_5_out, and_6_out, and_7_out, and_8_out, and_9_out, and_10_out, and_11_out, and_12_out, and_13_out, and_14_out, and_15_out);
  or or_2 (S1, and_16_out, and_17_out, and_18_out, and_19_out, and_20_out, and_21_out, and_22_out, and_23_out);
  or or_3 (S2, and_24_out, and_25_out, and_26_out, and_27_out, and_28_out, and_29_out, and_30_out, and_31_out, and_32_out, and_33_out, and_34_out);
  or or_4 (S3, and_35_out, and_36_out, and_37_out, and_38_out, and_39_out, and_40_out, and_41_out, and_42_out, and_43_out);
endmodule

module CONTROLSIGNAL (
  input  OP2,
  input  OP3,
  input  OP4,
  input  OP5,
  input  OP6,
  input  F12,
  input  F13,
  input  F14,
  input  F25,
  input  F30,
  output MemToReg,
  output MemWrite,
  output ALU_SRC,
  output RegWrite,
  output ecall,
  output S_Type,
  output BEQ,
  output BNE,
  output JALR,
  output JAL,
  output half,
  output CSR
);

  wire and_1_out, and_2_out, and_4_out, and_5_out, and_6_out, and_7_out, and_8_out, and_9_out, and_10_out,
       and_11_out, and_12_out, and_13_out, and_14_out, and_15_out, and_16_out, and_17_out, and_18_out,
       and_19_out, and_20_out, and_21_out, and_22_out, and_23_out, and_24_out, and_25_out, and_26_out,
       and_27_out, and_28_out, and_29_out, and_30_out, and_31_out, not_1_out, not_2_out, not_3_out,
       not_4_out, not_5_out, not_6_out, not_7_out, not_8_out, not_9_out, not_10_out, not_11_out, not_12_out,
       not_13_out, not_14_out, not_15_out, not_16_out, not_17_out, not_18_out, not_19_out, not_20_out,
       not_21_out, not_22_out, not_23_out, not_24_out, not_25_out, not_26_out, not_27_out, not_28_out,
       not_29_out, not_30_out, not_31_out, not_32_out, not_33_out, not_34_out, not_35_out, not_36_out,
       not_37_out, not_38_out, not_39_out, not_40_out, not_41_out, not_42_out, not_43_out, not_44_out,
       not_45_out, not_46_out, not_47_out, not_48_out, not_49_out, not_50_out, not_51_out, not_52_out,
       not_53_out, not_54_out, not_55_out, not_56_out, not_57_out, not_58_out, not_59_out, not_60_out,
       not_61_out, not_62_out, not_63_out, not_64_out, not_65_out, not_66_out, not_67_out, not_68_out,
       not_69_out, not_70_out, not_71_out, not_72_out, not_73_out, not_74_out, not_75_out, not_76_out,
       not_77_out, not_78_out, not_79_out, not_80_out, not_81_out, not_82_out, not_83_out, not_84_out,
       not_85_out, not_86_out, not_87_out, not_88_out, not_89_out, not_90_out, not_91_out, not_92_out,
       not_93_out, not_94_out, not_95_out, not_96_out, not_97_out, not_98_out, not_99_out, not_100_out,
       not_101_out, not_102_out, not_103_out, not_104_out, not_105_out, not_106_out, not_107_out,
       not_108_out, not_109_out, not_110_out, not_111_out, not_112_out, not_113_out, not_114_out,
       not_115_out, not_116_out, not_117_out, not_118_out, not_119_out, not_120_out, not_121_out,
       not_122_out, not_123_out, not_124_out, not_125_out, not_126_out, not_127_out, not_128_out,
       not_129_out, not_130_out, not_131_out, not_132_out, not_133_out, not_134_out, not_135_out,
       not_136_out, not_137_out, not_138_out, not_139_out, not_140_out, not_141_out, not_142_out,
       not_143_out, not_144_out, not_145_out, not_146_out, not_147_out, not_148_out, not_149_out,
       not_150_out, not_151_out, not_152_out, not_153_out, not_154_out, not_155_out, not_156_out,
       not_157_out, not_158_out, not_159_out, not_160_out, not_161_out, not_162_out, not_163_out,
       not_164_out, not_165_out, not_166_out, not_167_out, not_168_out, not_169_out, not_170_out,
       not_171_out, not_172_out, not_173_out, not_174_out, not_175_out, not_176_out, not_177_out,
       not_178_out, not_179_out, not_180_out, not_181_out, not_182_out, not_183_out, not_184_out,
       not_185_out, not_186_out, not_187_out, not_188_out, not_189_out, not_190_out, not_191_out,
       not_192_out, not_193_out, not_194_out, not_195_out, not_196_out, not_197_out, not_198_out,
       not_199_out, not_200_out, not_201_out, not_202_out, not_203_out, not_204_out, not_205_out,
       not_206_out, not_207_out, not_208_out, not_209_out, not_210_out, not_211_out, not_212_out,
       not_213_out, not_214_out, not_215_out, not_216_out;

  not not_1 (not_1_out, OP2);
  not not_2 (not_2_out, OP3);
  not not_3 (not_3_out, OP4);
  not not_4 (not_4_out, OP5);
  not not_5 (not_5_out, OP6);
  not not_6 (not_6_out, F12);
  not not_7 (not_7_out, F14);
  not not_8 (not_8_out, OP2);
  not not_9 (not_9_out, OP3);
  not not_10 (not_10_out, OP4);
  not not_11 (not_11_out, OP5);
  not not_12 (not_12_out, OP6);
  not not_13 (not_13_out, F13);
  not not_14 (not_14_out, OP2);
  not not_15 (not_15_out, OP3);
  not not_16 (not_16_out, OP4);
  not not_17 (not_17_out, OP6);
  not not_18 (not_18_out, F12);
  not not_19 (not_19_out, F14);
  not not_20 (not_20_out, OP2);
  not not_21 (not_21_out, OP3);
  not not_22 (not_22_out, OP4);
  not not_23 (not_23_out, OP6);
  not not_24 (not_24_out, F12);
  not not_25 (not_25_out, F14);
  not not_26 (not_26_out, OP2);
  not not_27 (not_27_out, OP3);
  not not_28 (not_28_out, OP4);
  not not_29 (not_29_out, OP5);
  not not_30 (not_30_out, OP6);
  not not_31 (not_31_out, F13);
  not not_32 (not_32_out, OP2);
  not not_33 (not_33_out, OP3);
  not not_34 (not_34_out, OP5);
  not not_35 (not_35_out, OP6);
  not not_36 (not_36_out, F12);
  not not_37 (not_37_out, OP2);
  not not_38 (not_38_out, OP3);
  not not_39 (not_39_out, OP5);
  not not_40 (not_40_out, OP6);
  not not_41 (not_41_out, F13);
  not not_42 (not_42_out, F25);
  not not_43 (not_43_out, F30);
  not not_44 (not_44_out, OP2);
  not not_45 (not_45_out, OP3);
  not not_46 (not_46_out, OP5);
  not not_47 (not_47_out, OP6);
  not not_48 (not_48_out, F25);
  not not_49 (not_49_out, OP2);
  not not_50 (not_50_out, OP3);
  not not_51 (not_51_out, OP5);
  not not_52 (not_52_out, OP6);
  not not_53 (not_53_out, OP2);
  not not_54 (not_54_out, OP3);
  not not_55 (not_55_out, OP3);
  not not_56 (not_56_out, OP4);
  not not_57 (not_57_out, F12);
  not not_58 (not_58_out, F13);
  not not_59 (not_59_out, F14);
  not not_60 (not_60_out, F30);
  not not_61 (not_61_out, F25);
  not not_62 (not_62_out, F14);
  not not_63 (not_63_out, F13);
  not not_64 (not_64_out, F12);
  not not_65 (not_65_out, OP6);
  not not_66 (not_66_out, OP3);
  not not_67 (not_67_out, OP2);
  not not_68 (not_68_out, F25);
  not not_69 (not_69_out, F14);
  not not_70 (not_70_out, F13);
  not not_71 (not_71_out, F12);
  not not_72 (not_72_out, OP6);
  not not_73 (not_73_out, OP3);
  not not_74 (not_74_out, OP2);
  not not_75 (not_75_out, F30);
  not not_76 (not_76_out, F25);
  not not_77 (not_77_out, OP6);
  not not_78 (not_78_out, OP3);
  not not_79 (not_79_out, OP2);
  not not_80 (not_80_out, F30);
  not not_81 (not_81_out, F25);
  not not_82 (not_82_out, F12);
  not not_83 (not_83_out, OP6);
  not not_84 (not_84_out, OP3);
  not not_85 (not_85_out, OP2);
  not not_86 (not_86_out, F30);
  not not_87 (not_87_out, F25);
  not not_88 (not_88_out, F14);
  not not_89 (not_89_out, F12);
  not not_90 (not_90_out, OP6);
  not not_91 (not_91_out, OP3);
  not not_92 (not_92_out, OP2);
  not not_93 (not_93_out, F30);
  not not_94 (not_94_out, F25);
  not not_95 (not_95_out, F14);
  not not_96 (not_96_out, OP6);
  not not_97 (not_97_out, OP3);
  not not_98 (not_98_out, OP2);
  not not_99 (not_99_out, F14);
  not not_100 (not_100_out, F13);
  not not_101 (not_101_out, F12);
  not not_102 (not_102_out, OP6);
  not not_103 (not_103_out, OP5);
  not not_104 (not_104_out, OP3);
  not not_105 (not_105_out, OP2);
  not not_106 (not_106_out, OP6);
  not not_107 (not_107_out, OP5);
  not not_108 (not_108_out, OP3);
  not not_109 (not_109_out, OP2);
  not not_110 (not_110_out, F12);
  not not_111 (not_111_out, OP6);
  not not_112 (not_112_out, OP5);
  not not_113 (not_113_out, OP3);
  not not_114 (not_114_out, OP2);
  not not_115 (not_115_out, F13);
  not not_116 (not_116_out, F12);
  not not_117 (not_117_out, OP6);
  not not_118 (not_118_out, OP5);
  not not_119 (not_119_out, OP3);
  not not_120 (not_120_out, OP2);
  not not_121 (not_121_out, F14);
  not not_122 (not_122_out, F12);
  not not_123 (not_123_out, OP6);
  not not_124 (not_124_out, OP5);
  not not_125 (not_125_out, OP3);
  not not_126 (not_126_out, OP2);
  not not_127 (not_127_out, F30);
  not not_128 (not_128_out, F25);
  not not_129 (not_129_out, F14);
  not not_130 (not_130_out, F13);
  not not_131 (not_131_out, OP6);
  not not_132 (not_132_out, OP5);
  not not_133 (not_133_out, OP3);
  not not_134 (not_134_out, OP2);
  not not_135 (not_135_out, F30);
  not not_136 (not_136_out, F25);
  not not_137 (not_137_out, F13);
  not not_138 (not_138_out, OP6);
  not not_139 (not_139_out, OP5);
  not not_140 (not_140_out, OP3);
  not not_141 (not_141_out, OP2);
  not not_142 (not_142_out, F25);
  not not_143 (not_143_out, F13);
  not not_144 (not_144_out, OP6);
  not not_145 (not_145_out, OP5);
  not not_146 (not_146_out, OP3);
  not not_147 (not_147_out, OP2);
  not not_148 (not_148_out, F14);
  not not_149 (not_149_out, F12);
  not not_150 (not_150_out, OP6);
  not not_151 (not_151_out, OP5);
  not not_152 (not_152_out, OP4);
  not not_153 (not_153_out, OP3);
  not not_154 (not_154_out, OP2);
  not not_155 (not_155_out, OP4);
  not not_156 (not_156_out, F14);
  not not_157 (not_157_out, F13);
  not not_158 (not_158_out, F12);
  not not_159 (not_159_out, OP4);
  not not_160 (not_160_out, OP3);
  not not_161 (not_161_out, F30);
  not not_162 (not_162_out, F25);
  not not_163 (not_163_out, F14);
  not not_164 (not_164_out, F13);
  not not_165 (not_165_out, OP6);
  not not_166 (not_166_out, OP3);
  not not_167 (not_167_out, OP2);
  not not_168 (not_168_out, F30);
  not not_169 (not_169_out, F25);
  not not_170 (not_170_out, F13);
  not not_171 (not_171_out, F12);
  not not_172 (not_172_out, OP6);
  not not_173 (not_173_out, OP3);
  not not_174 (not_174_out, OP2);
  not not_175 (not_175_out, F13);
  not not_176 (not_176_out, OP6);
  not not_177 (not_177_out, OP5);
  not not_178 (not_178_out, OP4);
  not not_179 (not_179_out, OP3);
  not not_180 (not_180_out, OP2);
  not not_181 (not_181_out, OP2);
  not not_182 (not_182_out, OP3);
  not not_183 (not_183_out, F12);
  not not_184 (not_184_out, F13);
  not not_185 (not_185_out, F14);
  not not_186 (not_186_out, OP2);
  not not_187 (not_187_out, OP3);
  not not_188 (not_188_out, OP4);
  not not_189 (not_189_out, OP6);
  not not_190 (not_190_out, F12);
  not not_191 (not_191_out, F14);
  not not_192 (not_192_out, OP2);
  not not_193 (not_193_out, OP3);
  not not_194 (not_194_out, OP4);
  not not_195 (not_195_out, F12);
  not not_196 (not_196_out, F13);
  not not_197 (not_197_out, F14);
  not not_198 (not_198_out, OP2);
  not not_199 (not_199_out, OP3);
  not not_200 (not_200_out, OP4);
  not not_201 (not_201_out, F13);
  not not_202 (not_202_out, F14);
  not not_203 (not_203_out, OP3);
  not not_204 (not_204_out, OP4);
  not not_205 (not_205_out, F12);
  not not_206 (not_206_out, F13);
  not not_207 (not_207_out, F14);
  not not_208 (not_208_out, OP4);
  not not_209 (not_209_out, OP2);
  not not_210 (not_210_out, OP3);
  not not_211 (not_211_out, OP4);
  not not_212 (not_212_out, OP5);
  not not_213 (not_213_out, OP6);
  not not_214 (not_214_out, F13);
  not not_215 (not_215_out, OP2);
  not not_216 (not_216_out, OP3);
  and and_1 (and_1_out, not_1_out, not_2_out, not_3_out, not_4_out, not_5_out, not_6_out, F13, not_7_out);
  and and_2 (and_2_out, not_8_out, not_9_out, not_10_out, not_11_out, not_12_out, F12, not_13_out, F14);
  and and_3 (MemWrite, not_14_out, not_15_out, not_16_out, OP5, not_17_out, not_18_out, F13, not_19_out);
  and and_4 (and_4_out, not_20_out, not_21_out, not_22_out, not_23_out, not_24_out, F13, not_25_out);
  and and_5 (and_5_out, not_26_out, not_27_out, not_28_out, not_29_out, not_30_out, F12, not_31_out, F14);
  and and_6 (and_6_out, not_32_out, not_33_out, OP4, not_34_out, not_35_out, not_36_out);
  and and_7 (and_7_out, not_37_out, not_38_out, OP4, not_39_out, not_40_out, not_41_out, not_42_out, not_43_out);
  and and_8 (and_8_out, not_44_out, not_45_out, OP4, not_46_out, not_47_out, F14, not_48_out);
  and and_9 (and_9_out, not_49_out, not_50_out, OP4, not_51_out, not_52_out, F13, F14);
  and and_10 (and_10_out, not_53_out, not_54_out, OP4, OP5, OP6, F13, F14);
  and and_11 (and_11_out, OP2, not_55_out, not_56_out, OP5, OP6, not_57_out, not_58_out, not_59_out);
  and and_12 (and_12_out, not_60_out, not_61_out, not_62_out, not_63_out, not_64_out, not_65_out, OP5, OP4, not_66_out, not_67_out);
  and and_13 (and_13_out, F30, not_68_out, not_69_out, not_70_out, not_71_out, not_72_out, OP5, OP4, not_73_out, not_74_out);
  and and_14 (and_14_out, not_75_out, not_76_out, F14, F13, F12, not_77_out, OP5, OP4, not_78_out, not_79_out);
  and and_15 (and_15_out, not_80_out, not_81_out, F14, F13, not_82_out, not_83_out, OP5, OP4, not_84_out, not_85_out);
  and and_16 (and_16_out, not_86_out, not_87_out, not_88_out, F13, not_89_out, not_90_out, OP5, OP4, not_91_out, not_92_out);
  and and_17 (and_17_out, not_93_out, not_94_out, not_95_out, F13, F12, not_96_out, OP5, OP4, not_97_out, not_98_out);
  and and_18 (and_18_out, not_99_out, not_100_out, not_101_out, not_102_out, not_103_out, OP4, not_104_out, not_105_out);
  and and_19 (and_19_out, F14, F13, F12, not_106_out, not_107_out, OP4, not_108_out, not_109_out);
  and and_20 (and_20_out, F14, F13, not_110_out, not_111_out, not_112_out, OP4, not_113_out, not_114_out);
  and and_21 (and_21_out, F14, not_115_out, not_116_out, not_117_out, not_118_out, OP4, not_119_out, not_120_out);
  and and_22 (and_22_out, not_121_out, F13, not_122_out, not_123_out, not_124_out, OP4, not_125_out, not_126_out);
  and and_23 (and_23_out, not_127_out, not_128_out, not_129_out, not_130_out, F12, not_131_out, not_132_out, OP4, not_133_out, not_134_out);
  and and_24 (and_24_out, not_135_out, not_136_out, F14, not_137_out, F12, not_138_out, not_139_out, OP4, not_140_out, not_141_out);
  and and_25 (and_25_out, F30, not_142_out, F14, not_143_out, F12, not_144_out, not_145_out, OP4, not_146_out, not_147_out);
  and and_26 (and_26_out, not_148_out, F13, not_149_out, not_150_out, not_151_out, not_152_out, not_153_out, not_154_out);
  and and_27 (and_27_out, OP6, OP5, not_155_out, OP3, OP2);
  and and_28 (and_28_out, not_156_out, not_157_out, not_158_out, OP6, OP5, not_159_out, not_160_out, OP2);
  and and_29 (and_29_out, not_161_out, not_162_out, not_163_out, not_164_out, F12, not_165_out, OP5, OP4, not_166_out, not_167_out);
  and and_30 (and_30_out, not_168_out, not_169_out, F14, not_170_out, not_171_out, not_172_out, OP5, OP4, not_173_out, not_174_out);
  and and_31 (and_31_out, F14, not_175_out, F12, not_176_out, not_177_out, not_178_out, not_179_out, not_180_out);
  and and_32 (ecall, not_181_out, not_182_out, OP4, OP5, OP6, not_183_out, not_184_out, not_185_out);
  and and_33 (S_Type, not_186_out, not_187_out, not_188_out, OP5, not_189_out, not_190_out, F13, not_191_out);
  and and_34 (BEQ, not_192_out, not_193_out, not_194_out, OP5, OP6, not_195_out, not_196_out, not_197_out);
  and and_35 (BNE, not_198_out, not_199_out, not_200_out, OP5, OP6, F12, not_201_out, not_202_out);
  and and_36 (JALR, OP2, not_203_out, not_204_out, OP5, OP6, not_205_out, not_206_out, not_207_out);
  and and_37 (JAL, OP2, OP3, not_208_out, OP5, OP6);
  and and_38 (half, not_209_out, not_210_out, not_211_out, not_212_out, not_213_out, F12, not_214_out, F14);
  and and_39 (CSR, not_215_out, not_216_out, OP4, OP5, OP6, F13, F14);
  or or_1 (MemToReg, and_1_out, and_2_out);
  or or_2 (ALU_SRC, and_4_out, and_5_out, and_6_out, and_7_out, and_8_out, and_9_out, and_10_out, and_11_out);
  or or_3 (RegWrite, and_12_out, and_13_out, and_14_out, and_15_out, and_16_out, and_17_out, and_18_out, and_19_out, and_20_out, and_21_out, and_22_out, and_23_out, and_24_out, and_25_out, and_26_out, and_27_out, and_28_out, and_29_out, and_30_out, and_31_out);
endmodule

module ALU (
  input  [31:0] X,
  input  [31:0] Y,
  input  [3:0] AluOP,
  output NOTLESS,
  output Equal,
  output [31:0] Result,
  output [31:0] Result_2,
  output LESS
);

  wire [0:0] comparator_1_lt, comparator_2_lt;
  wire [31:0] adder_1_out, AND_out, NOR_out, OR_out, shifter_1_out, shifter_2_out, shifter_3_out,
       subtractor_1_out, XOR_out;

  assign AND_out = X & Y;  // AND_Gate AND, 32 bits wide
  assign OR_out = X | Y;  // OR_Gate OR, 32 bits wide
  Shifter #(.width(32), .shift("ll")) shifter_1 (.in(X), .\dist (Y[4:0]), .out(shifter_1_out));
  Shifter #(.width(32), .shift("ar")) shifter_2 (.in(X), .\dist (Y[4:0]), .out(shifter_2_out));
  Shifter #(.width(32), .shift("lr")) shifter_3 (.in(X), .\dist (Y[4:0]), .out(shifter_3_out));
  Adder #(.width(32)) adder_1 (.a(X), .b(Y), .out(adder_1_out), .cin(1'b0));  // open: cout
  Subtractor #(.width(32)) subtractor_1 (.a(X), .b(Y), .out(subtractor_1_out), .bin(1'b0));  // open: bout
  assign XOR_out = X ^ Y;  // XOR_Gate XOR, 32 bits wide
  assign NOR_out = ~(X | Y);  // NOR_Gate NOR, 32 bits wide
  Comparator #(.width(32), .mode("twosComplement")) comparator_1 (
    .a(X), .b(Y), .eq(Equal), .lt(comparator_1_lt[0]));  // open: gt
  Comparator #(.width(32), .mode("unsigned")) comparator_2 (.a(X), .b(Y), .lt(comparator_2_lt[0]));  // open: gt, eq
  Multiplexer #(.select(4), .width(32), .disabled(0), .enable("false")) multiplexer_1 (
    .in0(shifter_1_out), .in1(shifter_2_out), .in2(shifter_3_out), .in3({32{1'b0}}), .in4({32{1'b0}}),
    .in5(adder_1_out), .in6(subtractor_1_out), .in7(AND_out), .in8(OR_out), .in9(XOR_out), .in10(NOR_out),
    .in11({{31{1'b0}}, comparator_1_lt[0]}), .in12({{31{1'b0}}, comparator_2_lt[0]}), .in13({32{1'b0}}),
    .in14({32{1'b0}}), .in15({32{1'b0}}), .out(Result), .sel(AluOP));
  Multiplexer #(.select(4), .width(32), .disabled(0), .enable("false")) multiplexer_2 (
    .in0({32{1'b0}}), .in1({32{1'b0}}), .in2({32{1'b0}}), .in3({32{1'b0}}), .in4({32{1'b0}}),
    .in5({32{1'b0}}), .in6({32{1'b0}}), .in7({32{1'b0}}), .in8({32{1'b0}}), .in9({32{1'b0}}),
    .in10({32{1'b0}}), .in11({32{1'b0}}), .in12({32{1'b0}}), .in13({32{1'b0}}), .in14({32{1'b0}}),
    .in15({32{1'b0}}), .out(Result_2), .sel(AluOP));
  Multiplexer #(.select(4), .width(1), .disabled(0), .enable("false")) multiplexer_3 (
    .in0(1'b0), .in1(1'b0), .in2(1'b0), .in3(1'b0), .in4(1'b0), .in5(1'b0), .in6(1'b0), .in7(1'b0),
    .in8(1'b0), .in9(1'b0), .in10(1'b0), .in11(comparator_1_lt[0]), .in12(comparator_2_lt[0]), .in13(1'b0),
    .in14(1'b0), .in15(1'b0), .out(LESS), .sel(AluOP));
  not not_1 (NOTLESS, LESS);

  // Other names for the same wires on the sheet: Result2[31:0] = Result_2; S[3:0] = AluOP
endmodule

module REGIFILE (
  input  [31:0] Din,
  input  Clk,
  input  WE,
  input  [4:0] R1Adr,
  input  [4:0] WAdr,
  input  [4:0] R2Adr,
  output [31:0] R1,
  output [31:0] R2
);

  // RegisterFile registerfile_1: pin names not known; wires that end beside it: Din, Clk, WE, WAdr, R1Adr, R2Adr, R1, R2
endmodule

module MAZEMAP (
  input  WE,
  input  [9:0] Addr,
  input  CLK,
  input  RST,
  input  [31:0] Data,
  output [31:0] R1,
  output [31:0] R9,
  output [31:0] R17,
  output [31:0] R25,
  output [31:0] R2,
  output [31:0] R10,
  output [31:0] R18,
  output [31:0] R26,
  output [31:0] R3,
  output [31:0] R11,
  output [31:0] R19,
  output [31:0] R27,
  output [31:0] R4,
  output [31:0] R12,
  output [31:0] R20,
  output [31:0] R28,
  output [31:0] R5,
  output [31:0] R13,
  output [31:0] R21,
  output [31:0] R29,
  output [31:0] R6,
  output [31:0] R14,
  output [31:0] R22,
  output [31:0] R30,
  output [31:0] R7,
  output [31:0] R15,
  output [31:0] R23,
  output [31:0] R31,
  output [31:0] R8,
  output [31:0] R16,
  output [31:0] R24,
  output [31:0] R32
);

  wire and_1_out, and_2_out, and_3_out, and_4_out, and_5_out, and_6_out, and_7_out, and_8_out, and_9_out,
       and_10_out, and_11_out, and_12_out, and_13_out, and_14_out, and_15_out, and_16_out, and_17_out,
       and_18_out, and_19_out, and_20_out, and_21_out, and_22_out, and_23_out, and_24_out, and_25_out,
       and_26_out, and_27_out, and_28_out, and_29_out, and_30_out, and_31_out, and_32_out, L1, L2, L3, L4,
       L5, L6, L7, L8, L9, L10, L11, L12, L13, L14, L15, L16, L17, L18, L19, L20, L21, L22, L23, L24, L25,
       L26, L27, L28, L29, L30, L31, L32;

  and and_1 (and_1_out, WE, L1);
  and and_2 (and_2_out, WE, L2);
  and and_3 (and_3_out, WE, L3);
  and and_4 (and_4_out, WE, L4);
  and and_5 (and_5_out, WE, L5);
  and and_6 (and_6_out, WE, L6);
  and and_7 (and_7_out, WE, L7);
  and and_8 (and_8_out, WE, L8);
  Register #(.width(32), .trigger("rising"), .Select("low")) register_1 (
    .D(Data), .en(and_1_out), .Q(R1), .clk(CLK), .clr(RST), .cs(1'b0), .preset(1'b0));
  Register #(.width(32), .trigger("rising"), .Select("low")) register_2 (
    .D(Data), .en(and_2_out), .Q(R2), .clk(CLK), .clr(RST), .cs(1'b0), .preset(1'b0));
  Register #(.width(32), .trigger("rising"), .Select("low")) register_3 (
    .D(Data), .en(and_3_out), .Q(R3), .clk(CLK), .clr(RST), .cs(1'b0), .preset(1'b0));
  Register #(.width(32), .trigger("rising"), .Select("low")) register_4 (
    .D(Data), .en(and_4_out), .Q(R4), .clk(CLK), .clr(RST), .cs(1'b0), .preset(1'b0));
  Register #(.width(32), .trigger("rising"), .Select("low")) register_5 (
    .D(Data), .en(and_5_out), .Q(R5), .clk(CLK), .clr(RST), .cs(1'b0), .preset(1'b0));
  Register #(.width(32), .trigger("rising"), .Select("low")) register_6 (
    .D(Data), .en(and_6_out), .Q(R6), .clk(CLK), .clr(RST), .cs(1'b0), .preset(1'b0));
  Register #(.width(32), .trigger("rising"), .Select("low")) register_7 (
    .D(Data), .en(and_7_out), .Q(R7), .clk(CLK), .clr(RST), .cs(1'b0), .preset(1'b0));
  Register #(.width(32), .trigger("rising"), .Select("low")) register_8 (
    .D(Data), .en(and_8_out), .Q(R8), .clk(CLK), .clr(RST), .cs(1'b0), .preset(1'b0));
  and and_9 (and_9_out, WE, L9);
  and and_10 (and_10_out, WE, L10);
  and and_11 (and_11_out, WE, L11);
  and and_12 (and_12_out, WE, L12);
  and and_13 (and_13_out, WE, L13);
  and and_14 (and_14_out, WE, L14);
  and and_15 (and_15_out, WE, L15);
  and and_16 (and_16_out, WE, L16);
  Register #(.width(32), .trigger("rising"), .Select("low")) register_9 (
    .D(Data), .en(and_9_out), .Q(R9), .clk(CLK), .clr(RST), .cs(1'b0), .preset(1'b0));
  Register #(.width(32), .trigger("rising"), .Select("low")) register_10 (
    .D(Data), .en(and_10_out), .Q(R10), .clk(CLK), .clr(RST), .cs(1'b0), .preset(1'b0));
  Register #(.width(32), .trigger("rising"), .Select("low")) register_11 (
    .D(Data), .en(and_11_out), .Q(R11), .clk(CLK), .clr(RST), .cs(1'b0), .preset(1'b0));
  Register #(.width(32), .trigger("rising"), .Select("low")) register_12 (
    .D(Data), .en(and_12_out), .Q(R12), .clk(CLK), .clr(RST), .cs(1'b0), .preset(1'b0));
  Register #(.width(32), .trigger("rising"), .Select("low")) register_13 (
    .D(Data), .en(and_13_out), .Q(R13), .clk(CLK), .clr(RST), .cs(1'b0), .preset(1'b0));
  Register #(.width(32), .trigger("rising"), .Select("low")) register_14 (
    .D(Data), .en(and_14_out), .Q(R14), .clk(CLK), .clr(RST), .cs(1'b0), .preset(1'b0));
  Register #(.width(32), .trigger("rising"), .Select("low")) register_15 (
    .D(Data), .en(and_15_out), .Q(R15), .clk(CLK), .clr(RST), .cs(1'b0), .preset(1'b0));
  Register #(.width(32), .trigger("rising"), .Select("low")) register_16 (
    .D(Data), .en(and_16_out), .Q(R16), .clk(CLK), .clr(RST), .cs(1'b0), .preset(1'b0));
  and and_17 (and_17_out, WE, L17);
  and and_18 (and_18_out, WE, L18);
  and and_19 (and_19_out, WE, L19);
  and and_20 (and_20_out, WE, L20);
  and and_21 (and_21_out, WE, L21);
  and and_22 (and_22_out, WE, L22);
  and and_23 (and_23_out, WE, L23);
  and and_24 (and_24_out, WE, L24);
  Register #(.width(32), .trigger("rising"), .Select("low")) register_17 (
    .D(Data), .en(and_17_out), .Q(R17), .clk(CLK), .clr(RST), .cs(1'b0), .preset(1'b0));
  Register #(.width(32), .trigger("rising"), .Select("low")) register_18 (
    .D(Data), .en(and_18_out), .Q(R18), .clk(CLK), .clr(RST), .cs(1'b0), .preset(1'b0));
  Register #(.width(32), .trigger("rising"), .Select("low")) register_19 (
    .D(Data), .en(and_19_out), .Q(R19), .clk(CLK), .clr(RST), .cs(1'b0), .preset(1'b0));
  Register #(.width(32), .trigger("rising"), .Select("low")) register_20 (
    .D(Data), .en(and_20_out), .Q(R20), .clk(CLK), .clr(RST), .cs(1'b0), .preset(1'b0));
  Register #(.width(32), .trigger("rising"), .Select("low")) register_21 (
    .D(Data), .en(and_21_out), .Q(R21), .clk(CLK), .clr(RST), .cs(1'b0), .preset(1'b0));
  Register #(.width(32), .trigger("rising"), .Select("low")) register_22 (
    .D(Data), .en(and_22_out), .Q(R22), .clk(CLK), .clr(RST), .cs(1'b0), .preset(1'b0));
  Register #(.width(32), .trigger("rising"), .Select("low")) register_23 (
    .D(Data), .en(and_23_out), .Q(R23), .clk(CLK), .clr(RST), .cs(1'b0), .preset(1'b0));
  Register #(.width(32), .trigger("rising"), .Select("low")) register_24 (
    .D(Data), .en(and_24_out), .Q(R24), .clk(CLK), .clr(RST), .cs(1'b0), .preset(1'b0));
  and and_25 (and_25_out, WE, L25);
  and and_26 (and_26_out, WE, L26);
  and and_27 (and_27_out, WE, L27);
  and and_28 (and_28_out, WE, L28);
  and and_29 (and_29_out, WE, L29);
  and and_30 (and_30_out, WE, L30);
  and and_31 (and_31_out, WE, L31);
  and and_32 (and_32_out, WE, L32);
  Register #(.width(32), .trigger("rising"), .Select("low")) register_25 (
    .D(Data), .en(and_25_out), .Q(R25), .clk(CLK), .clr(RST), .cs(1'b0), .preset(1'b0));
  Register #(.width(32), .trigger("rising"), .Select("low")) register_26 (
    .D(Data), .en(and_26_out), .Q(R26), .clk(CLK), .clr(RST), .cs(1'b0), .preset(1'b0));
  Register #(.width(32), .trigger("rising"), .Select("low")) register_27 (
    .D(Data), .en(and_27_out), .Q(R27), .clk(CLK), .clr(RST), .cs(1'b0), .preset(1'b0));
  Register #(.width(32), .trigger("rising"), .Select("low")) register_28 (
    .D(Data), .en(and_28_out), .Q(R28), .clk(CLK), .clr(RST), .cs(1'b0), .preset(1'b0));
  Register #(.width(32), .trigger("rising"), .Select("low")) register_29 (
    .D(Data), .en(and_29_out), .Q(R29), .clk(CLK), .clr(RST), .cs(1'b0), .preset(1'b0));
  Register #(.width(32), .trigger("rising"), .Select("low")) register_30 (
    .D(Data), .en(and_30_out), .Q(R30), .clk(CLK), .clr(RST), .cs(1'b0), .preset(1'b0));
  Register #(.width(32), .trigger("rising"), .Select("low")) register_31 (
    .D(Data), .en(and_31_out), .Q(R31), .clk(CLK), .clr(RST), .cs(1'b0), .preset(1'b0));
  Register #(.width(32), .trigger("rising"), .Select("low")) register_32 (
    .D(Data), .en(and_32_out), .Q(R32), .clk(CLK), .clr(RST), .cs(1'b0), .preset(1'b0));
  Demultiplexer #(.select(5), .width(1), .tristate("false"), .disabled(0), .enable("false")) demultiplexer_1 (
    .out0(L1), .out1(L2), .out2(L3), .out3(L4), .out4(L5), .out5(L6), .out6(L7), .out7(L8), .out8(L9),
    .out9(L10), .out10(L11), .out11(L12), .out12(L13), .out13(L14), .out14(L15), .out15(L16), .out16(L17),
    .out17(L18), .out18(L19), .out19(L20), .out20(L21), .out21(L22), .out22(L23), .out23(L24), .out24(L25),
    .out25(L26), .out26(L27), .out27(L28), .out28(L29), .out29(L30), .out30(L31), .out31(L32), .in(1'b1),
    .sel(Addr[4:0]));
endmodule

module DISPLAY (
  input  WE,
  input  [31:0] A1,
  input  [31:0] A2,
  input  [31:0] A3,
  input  [31:0] A4,
  input  [31:0] A5,
  input  [31:0] A6,
  input  [31:0] A7,
  input  [31:0] A8,
  input  [31:0] A9,
  input  [31:0] A10,
  input  [31:0] A11,
  input  [31:0] A12,
  input  [31:0] A13,
  input  [31:0] A14,
  input  [31:0] A15,
  input  [31:0] A16,
  input  [31:0] A17,
  input  [31:0] A18,
  input  [31:0] A19,
  input  [31:0] A20,
  input  [31:0] A21,
  input  [31:0] A22,
  input  [31:0] A23,
  input  [31:0] A24,
  input  [31:0] A25,
  input  [31:0] A26,
  input  [31:0] A27,
  input  [31:0] A28,
  input  [31:0] A29,
  input  [31:0] A30,
  input  [31:0] A31,
  input  [31:0] A32,
  input  CLK,
  input  RST,
  output [31:0] R1,
  output [31:0] R2,
  output [31:0] R3,
  output [31:0] R4,
  output [31:0] R5,
  output [31:0] R6,
  output [31:0] R7,
  output [31:0] R8,
  output [31:0] R9,
  output [31:0] R10,
  output [31:0] R11,
  output [31:0] R12,
  output [31:0] _13,
  output [31:0] R14,
  output [31:0] R15,
  output [31:0] R16,
  output [31:0] R17,
  output [31:0] R18,
  output [31:0] R19,
  output [31:0] R20,
  output [31:0] R21,
  output [31:0] R22,
  output [31:0] R23,
  output [31:0] R24,
  output [31:0] R25,
  output [31:0] R26,
  output [31:0] R27,
  output [31:0] R28,
  output [31:0] R29,
  output [31:0] R30,
  output [31:0] R31,
  output [31:0] R32
);

  Register #(.width(32), .trigger("rising"), .Select("low")) register_1 (
    .D(A1), .en(WE), .Q(R1), .clk(CLK), .clr(RST), .cs(1'b0), .preset(1'b0));
  Register #(.width(32), .trigger("rising"), .Select("low")) register_2 (
    .D(A5), .en(WE), .Q(R5), .clk(CLK), .clr(RST), .cs(1'b0), .preset(1'b0));
  Register #(.width(32), .trigger("rising"), .Select("low")) register_3 (
    .D(A9), .en(WE), .Q(R9), .clk(CLK), .clr(RST), .cs(1'b0), .preset(1'b0));
  Register #(.width(32), .trigger("rising"), .Select("low")) register_4 (
    .D(A13), .en(WE), .Q(_13), .clk(CLK), .clr(RST), .cs(1'b0), .preset(1'b0));
  Register #(.width(32), .trigger("rising"), .Select("low")) register_5 (
    .D(A17), .en(WE), .Q(R17), .clk(CLK), .clr(RST), .cs(1'b0), .preset(1'b0));
  Register #(.width(32), .trigger("rising"), .Select("low")) register_6 (
    .D(A21), .en(WE), .Q(R21), .clk(CLK), .clr(RST), .cs(1'b0), .preset(1'b0));
  Register #(.width(32), .trigger("rising"), .Select("low")) register_7 (
    .D(A25), .en(WE), .Q(R25), .clk(CLK), .clr(RST), .cs(1'b0), .preset(1'b0));
  Register #(.width(32), .trigger("rising"), .Select("low")) register_8 (
    .D(A29), .en(WE), .Q(R29), .clk(CLK), .clr(RST), .cs(1'b0), .preset(1'b0));
  Register #(.width(32), .trigger("rising"), .Select("low")) register_9 (
    .D(A2), .en(WE), .Q(R2), .clk(CLK), .clr(RST), .cs(1'b0), .preset(1'b0));
  Register #(.width(32), .trigger("rising"), .Select("low")) register_10 (
    .D(A6), .en(WE), .Q(R6), .clk(CLK), .clr(RST), .cs(1'b0), .preset(1'b0));
  Register #(.width(32), .trigger("rising"), .Select("low")) register_11 (
    .D(A10), .en(WE), .Q(R10), .clk(CLK), .clr(RST), .cs(1'b0), .preset(1'b0));
  Register #(.width(32), .trigger("rising"), .Select("low")) register_12 (
    .D(A14), .en(WE), .Q(R14), .clk(CLK), .clr(RST), .cs(1'b0), .preset(1'b0));
  Register #(.width(32), .trigger("rising"), .Select("low")) register_13 (
    .D(A18), .en(WE), .Q(R18), .clk(CLK), .clr(RST), .cs(1'b0), .preset(1'b0));
  Register #(.width(32), .trigger("rising"), .Select("low")) register_14 (
    .D(A22), .en(WE), .Q(R22), .clk(CLK), .clr(RST), .cs(1'b0), .preset(1'b0));
  Register #(.width(32), .trigger("rising"), .Select("low")) register_15 (
    .D(A26), .en(WE), .Q(R26), .clk(CLK), .clr(RST), .cs(1'b0), .preset(1'b0));
  Register #(.width(32), .trigger("rising"), .Select("low")) register_16 (
    .D(A30), .en(WE), .Q(R30), .clk(CLK), .clr(RST), .cs(1'b0), .preset(1'b0));
  Register #(.width(32), .trigger("rising"), .Select("low")) register_17 (
    .D(A3), .en(WE), .Q(R3), .clk(CLK), .clr(RST), .cs(1'b0), .preset(1'b0));
  Register #(.width(32), .trigger("rising"), .Select("low")) register_18 (
    .D(A7), .en(WE), .Q(R7), .clk(CLK), .clr(RST), .cs(1'b0), .preset(1'b0));
  Register #(.width(32), .trigger("rising"), .Select("low")) register_19 (
    .D(A11), .en(WE), .Q(R11), .clk(CLK), .clr(RST), .cs(1'b0), .preset(1'b0));
  Register #(.width(32), .trigger("rising"), .Select("low")) register_20 (
    .D(A15), .en(WE), .Q(R15), .clk(CLK), .clr(RST), .cs(1'b0), .preset(1'b0));
  Register #(.width(32), .trigger("rising"), .Select("low")) register_21 (
    .D(A19), .en(WE), .Q(R19), .clk(CLK), .clr(RST), .cs(1'b0), .preset(1'b0));
  Register #(.width(32), .trigger("rising"), .Select("low")) register_22 (
    .D(A23), .en(WE), .Q(R23), .clk(CLK), .clr(RST), .cs(1'b0), .preset(1'b0));
  Register #(.width(32), .trigger("rising"), .Select("low")) register_23 (
    .D(A27), .en(WE), .Q(R27), .clk(CLK), .clr(RST), .cs(1'b0), .preset(1'b0));
  Register #(.width(32), .trigger("rising"), .Select("low")) register_24 (
    .D(A31), .en(WE), .Q(R31), .clk(CLK), .clr(RST), .cs(1'b0), .preset(1'b0));
  Register #(.width(32), .trigger("rising"), .Select("low")) register_25 (
    .D(A4), .en(WE), .Q(R4), .clk(CLK), .clr(RST), .cs(1'b0), .preset(1'b0));
  Register #(.width(32), .trigger("rising"), .Select("low")) register_26 (
    .D(A8), .en(WE), .Q(R8), .clk(CLK), .clr(RST), .cs(1'b0), .preset(1'b0));
  Register #(.width(32), .trigger("rising"), .Select("low")) register_27 (
    .D(A12), .en(WE), .Q(R12), .clk(CLK), .clr(RST), .cs(1'b0), .preset(1'b0));
  Register #(.width(32), .trigger("rising"), .Select("low")) register_28 (
    .D(A16), .en(WE), .Q(R16), .clk(CLK), .clr(RST), .cs(1'b0), .preset(1'b0));
  Register #(.width(32), .trigger("rising"), .Select("low")) register_29 (
    .D(A20), .en(WE), .Q(R20), .clk(CLK), .clr(RST), .cs(1'b0), .preset(1'b0));
  Register #(.width(32), .trigger("rising"), .Select("low")) register_30 (
    .D(A24), .en(WE), .Q(R24), .clk(CLK), .clr(RST), .cs(1'b0), .preset(1'b0));
  Register #(.width(32), .trigger("rising"), .Select("low")) register_31 (
    .D(A28), .en(WE), .Q(R28), .clk(CLK), .clr(RST), .cs(1'b0), .preset(1'b0));
  Register #(.width(32), .trigger("rising"), .Select("low")) register_32 (
    .D(A32), .en(WE), .Q(R32), .clk(CLK), .clr(RST), .cs(1'b0), .preset(1'b0));
endmodule

module PLAYER (
);

  wire CLK, down, left, Level1, Level2, right, RST, up;
  wire [6:0] keyboard_1_data;
  wire [31:0] riscv_1_r1, riscv_1_r2, riscv_1_r3, riscv_1_r4, riscv_1_r5, riscv_1_r6, riscv_1_r7, riscv_1_r8,
       riscv_1_r9, riscv_1_r10, riscv_1_r11, riscv_1_r12, riscv_1_r13, riscv_1_r14, riscv_1_r15, riscv_1_r16,
       riscv_1_r17, riscv_1_r18, riscv_1_r19, riscv_1_r20, riscv_1_r21, riscv_1_r22, riscv_1_r23,
       riscv_1_r24, riscv_1_r25, riscv_1_r26, riscv_1_r27, riscv_1_r28, riscv_1_r29, riscv_1_r30,
       riscv_1_r31, riscv_1_r32;

  RISCV riscv_1 (
    .IRA(up), .IRB(down), .IRC(left), .IRD(right), .IRE(Level1), .IRF(Level2), .CLK(CLK), .RST(RST),
    .R1(riscv_1_r1), .R2(riscv_1_r2), .R3(riscv_1_r3), .R4(riscv_1_r4), .R5(riscv_1_r5), .R6(riscv_1_r6),
    .R7(riscv_1_r7), .R8(riscv_1_r8), .R9(riscv_1_r9), .R10(riscv_1_r10), .R11(riscv_1_r11),
    .R12(riscv_1_r12), .R13(riscv_1_r13), .R14(riscv_1_r14), .R15(riscv_1_r15), .R16(riscv_1_r16),
    .R17(riscv_1_r17), .R18(riscv_1_r18), .R19(riscv_1_r19), .R20(riscv_1_r20), .R21(riscv_1_r21),
    .R22(riscv_1_r22), .R23(riscv_1_r23), .R24(riscv_1_r24), .R25(riscv_1_r25), .R26(riscv_1_r26),
    .R27(riscv_1_r27), .R28(riscv_1_r28), .R29(riscv_1_r29), .R30(riscv_1_r30), .R31(riscv_1_r31),
    .R32(riscv_1_r32));  // open: GO, LEDDATA
  Button button_1 (.out(Level1));
  Button button_2 (.out(Level2));
  Button button_3 (.out(RST));
  Clock #(.highDuration(1), .lowDuration(1)) clock_1 (.out(CLK));
  DotMatrix #(.inputtype("row"), .matrixcols(32), .matrixrows(32), .persist(0), .dotshape("square")) dotmatrix_1 (
    .row0(riscv_1_r1), .row1(riscv_1_r2), .row2(riscv_1_r3), .row3(riscv_1_r4), .row4(riscv_1_r5),
    .row5(riscv_1_r6), .row6(riscv_1_r7), .row7(riscv_1_r8), .row8(riscv_1_r9), .row9(riscv_1_r10),
    .row10(riscv_1_r11), .row11(riscv_1_r12), .row12(riscv_1_r13), .row13(riscv_1_r14), .row14(riscv_1_r15),
    .row15(riscv_1_r16), .row16(riscv_1_r17), .row17(riscv_1_r18), .row18(riscv_1_r19), .row19(riscv_1_r20),
    .row20(riscv_1_r21), .row21(riscv_1_r22), .row22(riscv_1_r23), .row23(riscv_1_r24), .row24(riscv_1_r25),
    .row25(riscv_1_r26), .row26(riscv_1_r27), .row27(riscv_1_r28), .row28(riscv_1_r29), .row29(riscv_1_r30),
    .row30(riscv_1_r31), .row31(riscv_1_r32));
  Keyboard #(.Char_bit_width(7), .buflen(32), .trigger("rising")) keyboard_1 (
    .clk(CLK), .clr(RST), .data(keyboard_1_data));  // open: re, avail
  KEYBOARD keyboard_2 (
    .UP_W(up), .Down_S(down), .Left_A(left), .Right_D(right), .KeyBoardIn(keyboard_1_data), .CLK(CLK),
    .RST(RST));
endmodule

module KEYBOARD (
  input  [6:0] KeyBoardIn,
  input  CLK,
  input  RST,
  output UP_W,
  output Down_S,
  output Left_A,
  output Right_D
);

  wire comparator_1_eq, comparator_2_eq, comparator_3_eq, comparator_4_eq;

  Comparator #(.width(7), .mode("twosComplement")) comparator_1 (
    .a(KeyBoardIn), .b(7'b1110111), .eq(comparator_1_eq));  // open: gt, lt
  Comparator #(.width(7), .mode("twosComplement")) comparator_2 (
    .a(KeyBoardIn), .b(7'b1110011), .eq(comparator_2_eq));  // open: gt, lt
  Comparator #(.width(7), .mode("twosComplement")) comparator_3 (
    .a(KeyBoardIn), .b(7'b1100001), .eq(comparator_3_eq));  // open: gt, lt
  Comparator #(.width(7), .mode("twosComplement")) comparator_4 (
    .a(KeyBoardIn), .b(7'b1100100), .eq(comparator_4_eq));  // open: gt, lt
  Register #(.width(1), .trigger("rising"), .Select("low")) register_1 (
    .D(comparator_1_eq), .Q(UP_W), .clk(CLK), .clr(RST), .cs(1'b0), .preset(1'b0));  // open: en
  Register #(.width(1), .trigger("rising"), .Select("low")) register_2 (
    .D(comparator_2_eq), .Q(Down_S), .clk(CLK), .clr(RST), .cs(1'b0), .preset(1'b0));  // open: en
  Register #(.width(1), .trigger("rising"), .Select("low")) register_3 (
    .D(comparator_3_eq), .Q(Left_A), .clk(CLK), .clr(RST), .cs(1'b0), .preset(1'b0));  // open: en
  Register #(.width(1), .trigger("rising"), .Select("low")) register_4 (
    .D(comparator_4_eq), .Q(Right_D), .clk(CLK), .clr(RST), .cs(1'b0), .preset(1'b0));  // open: en
endmodule

module MUSIC (
  input  [15:0] Multiple,
  input  CLK,
  input  play,
  input  RST,
  output [13:0] R1,
  output Enable,
  output Volume,
  output [13:0] R2
);

  wire Now_CLK;
  wire [31:0] adder_1_out, PC_q;
  wire [31:14] MEM1_data, MEM2_data;

  Register #(.width(32), .trigger("rising"), .Select("low")) PC (
    .D(adder_1_out), .en(play), .Q(PC_q), .clk(Now_CLK), .clr(RST), .cs(1'b0), .preset(1'b0));
  FREQUENCY frequency_1 (.Multiple(Multiple), .before_CLK(CLK), .RST(RST), .after_CLK(Now_CLK));
  Adder #(.width(32)) adder_1 (.a(PC_q), .b(32'h4), .out(adder_1_out), .cout(RST));  // open: cin
  ROM #(.addrWidth(10), .dataWidth(32), .Select("low")) MEM1 (.addr(PC_q[11:2]), .data({MEM1_data, R1}));
  ROM #(.addrWidth(10), .dataWidth(32), .Select("low")) MEM2 (.addr(PC_q[11:2]), .data({MEM2_data, R2}));

  assign Enable = play;
  assign Volume = play;

  // Notes on the sheet:
  //   contents of MEM1 (hex, n*v repeats v):
  //   20b 20b 20b 0 20b 20b 20b 0 310 310 310 0 310 310 310 0 370 370 370 0 370 370 370 0 310 310 310 5*0
  //   2ba 2ba 2ba 0 2ba 2ba 2ba 0 293 293 293 0 293 293 293 0 24b 24b 24b 0 24b 24b 24b 0 20b 20b 20b 5*0
  //   310 310 310 0 310 310 310 0 2ba 2ba 2ba 0 2ba 2ba 2ba 0 293 293 293 0 293 293 293 0 24b 24b 24b 5*0
  //   310 310 310 0 310 310 310 0 2ba 2ba 2ba 0 2ba 2ba 2ba 0 293 293 293 0 293 293 293 0 24b 24b 24b 5*0
  //   20b 20b 20b 0 20b 20b 20b 0 310 310 310 0 310 310 310 0 370 370 370 0 370 370 370 0 310 310 310 5*0
  //   2ba 2ba 2ba 0 2ba 2ba 2ba 0 293 293 293 0 293 293 293 0 24b 24b 24b 0 24b 24b 24b 0 20b 20b 20b
  //   contents of MEM2 (hex, n*v repeats v):
  //   106 106 188 188 14a 14a 188 188 106 106 188 188 14a 14a 188 188 106 106 1b8 1b8 15d 15d 1b8 1b8 106
  //   106 188 188 14a 14a 188 188 e9 e9 188 188 126 126 188 188 106 106 188 188 14a 14a 188 188 e9 e9 188
  //   188 126 126 188 188 106 106 188 188 14a 14a 188 188 106 106 188 188 14a 14a 188 188 e9 e9 188 188
  //   126 126 188 188 106 106 188 188 14a 14a 188 188 e9 e9 188 188 126 126 188 188 106 106 188 188 14a
  //   14a 188 188 e9 e9 188 188 126 126 188 188 106 106 188 188 14a 14a 188 188 e9 e9 188 188 126 126 188
  //   188 106 106 188 188 14a 14a 188 188 106 106 188 188 14a 14a 188 188 106 106 1b8 1b8 15d 15d 1b8 1b8
  //   106 106 188 188 14a 14a 188 188 e9 e9 188 188 126 126 188 188 106 106 188 188 14a 14a 188 188 e9 e9
  //   188 188 126 126 188 188 106 106 188 188 14a 14a 188 188
endmodule

module FREQUENCY (
  input  [15:0] Multiple,
  input  before_CLK,
  input  RST,
  output after_CLK
);

  wire comparator_1_eq, comparator_2_eq, comparator_2_gt, or_1_out;
  wire [15:0] counter_1_q, shifter_1_out;

  Shifter #(.width(16), .shift("lr")) shifter_1 (.in(Multiple), .\dist (4'b0001), .out(shifter_1_out));
  Counter #(.width(16), .max('hffff), .ongoal("wrap"), .trigger("rising"), .behavior("new")) counter_1 (
    .load(comparator_1_eq), .D({16{1'b0}}), .count(1'b1), .Q(counter_1_q), .clk(before_CLK), .clr(RST),
    .preset(1'b0), .down(1'b0));  // open: carry
  Comparator #(.width(16), .mode("unsigned")) comparator_1 (
    .a(Multiple), .b(counter_1_q), .eq(comparator_1_eq));  // open: gt, lt
  Comparator #(.width(16), .mode("unsigned")) comparator_2 (
    .a(shifter_1_out), .b(counter_1_q), .gt(comparator_2_gt), .eq(comparator_2_eq));  // open: lt
  or or_1 (or_1_out, comparator_2_gt, comparator_2_eq);
  Multiplexer #(.select(1), .width(1), .disabled(0), .enable("false")) multiplexer_1 (
    .in0(1'b1), .in1(1'b0), .out(after_CLK), .sel(or_1_out));
endmodule
