// Logisim project 加法器.circ as structural Verilog: 5 circuits, main circuit 一位二进制半加器
module \一位二进制半加器  (
  input  A,
  input  B,
  output S,
  output C
);

  xor xor_1 (S, A, B);
  and and_1 (C, A, B);
endmodule

// 全加器
module \一位二进制全加器  (
  input  A,
  input  B,
  input  Ci,
  output S,
  output C0
);

  wire nand_1_out, nand_2_out, nand_3_out, xor_1_out;

  xor xor_1 (xor_1_out, A, B);
  nand nand_1 (nand_1_out, A, B);
  nand nand_2 (nand_2_out, A, Ci);
  nand nand_3 (nand_3_out, B, Ci);
  xor xor_2 (S, xor_1_out, Ci);
  nand nand_4 (C0, nand_1_out, nand_2_out, nand_3_out);
endmodule

module \串行进位并行加法器  (
  input  C0,
  input  A0,
  input  B0,
  input  A1,
  input  B1,
  input  A2,
  input  B2,
  input  A3,
  input  B3,
  output S0,
  output S1,
  output S2,
  output S3,
  output C4
);

  wire \一位二进制全加器_1_c0 , \一位二进制全加器_2_c0 , \一位二进制全加器_3_c0 ;

  \一位二进制全加器  \u_一位二进制全加器_1  (.A(C0), .B(A0), .Ci(B0), .S(S0), .C0(\一位二进制全加器_1_c0 ));
  \一位二进制全加器  \u_一位二进制全加器_2  (.A(\一位二进制全加器_1_c0 ), .B(A1), .Ci(B1), .S(S1), .C0(\一位二进制全加器_2_c0 ));
  \一位二进制全加器  \u_一位二进制全加器_3  (.A(\一位二进制全加器_2_c0 ), .B(A2), .Ci(B2), .S(S2), .C0(\一位二进制全加器_3_c0 ));
  \一位二进制全加器  \u_一位二进制全加器_4  (.A(\一位二进制全加器_3_c0 ), .B(A3), .Ci(B3), .S(S3), .C0(C4));
endmodule

module \先行进位并行加法器测试电路  (
  input  C0,
  input  A0,
  input  B0,
  input  A1,
  input  B1,
  input  A2,
  input  B2,
  input  A3,
  input  B3,
  output S0,
  output S1,
  output S2,
  output S3,
  output C4
);

  \先行进位并行加法器  \u_先行进位并行加法器_1  (
    .A0(A0), .B0(B0), .A1(A1), .B1(B1), .A2(A2), .B2(B2), .A3(A3), .B3(B3), .S0(S0), .S1(S1), .S2(S2),
    .S3(S3), .C4(C4), .C0(C0));
endmodule

module \先行进位并行加法器  (
  input  C0,
  input  A0,
  input  B0,
  input  A1,
  input  B1,
  input  A2,
  input  B2,
  input  A3,
  input  B3,
  output S0,
  output S1,
  output S2,
  output S3,
  output C4
);

  wire and_1_out, and_2_out, and_3_out, and_4_out, and_5_out, and_6_out, and_7_out, and_8_out, and_9_out,
       and_10_out, C1_out, C2_out, C3_out, P0_out, P1_out, P2_out, P3_out, Q0_out, Q1_out, Q2_out, Q3_out,
       xor_1_out, xor_2_out, xor_3_out, xor_4_out;

  and P0 (P0_out, A0, B0);
  or Q0 (Q0_out, A0, B0);
  and P1 (P1_out, A1, B1);
  or Q1 (Q1_out, B1, A1);
  and P2 (P2_out, A2, B2);
  or Q2 (Q2_out, B2, A2);
  and P3 (P3_out, A3, B3);
  or Q3 (Q3_out, B3, A3);
  and and_1 (and_1_out, C0, Q0_out);
  and and_2 (and_2_out, P0_out, Q1_out);
  and and_3 (and_3_out, C0, Q0_out, Q1_out);
  and and_4 (and_4_out, P1_out, Q2_out);
  and and_5 (and_5_out, Q2_out, Q1_out, P0_out);
  and and_6 (and_6_out, Q2_out, Q1_out, C0, Q0_out);
  and and_7 (and_7_out, P2_out, Q3_out);
  and and_8 (and_8_out, Q3_out, Q2_out, P1_out);
  and and_9 (and_9_out, P0_out, Q1_out, Q2_out, Q3_out);
  and and_10 (and_10_out, C0, Q0_out, Q1_out, Q2_out, Q3_out);
  or C1 (C1_out, P0_out, and_1_out);
  or C2 (C2_out, P1_out, and_2_out, and_3_out);
  or C3 (C3_out, P2_out, and_4_out, and_5_out, and_6_out);
  or u_C4 (C4, P3_out, and_7_out, and_8_out, and_9_out, and_10_out);
  xor xor_1 (xor_1_out, A0, B0);
  xor xor_2 (xor_2_out, A1, C1_out);
  xor xor_3 (xor_3_out, C2_out, A2);
  xor xor_4 (xor_4_out, C3_out, A3);
  xor xor_5 (S0, xor_1_out, C0);
  xor xor_6 (S1, xor_2_out, B1);
  xor xor_7 (S2, xor_3_out, B2);
  xor xor_8 (S3, xor_4_out, B3);
endmodule
