// Logisim project 实验5.circ as structural Verilog: 15 circuits, main circuit 四位二进制可逆计数器
module \四位二进制可逆计数器  (
  input  D,
  input  CPu,
  input  C,
  input  LD,
  input  CPd,
  input  B,
  input  CLR,
  input  A,
  output QD,
  output QC,
  output QB,
  output QA
);

  wire and_1_out, and_2_out, and_3_out, and_4_out, and_5_out, and_6_out, and_7_out, multiplexer_1_out,
       multiplexer_2_out, multiplexer_3_out, nor_1_out, nor_2_out, nor_3_out, nor_4_out, not_1_out,
       not_2_out, not_3_out, not_4_out, or_1_out, or_2_out, or_3_out, or_4_out, or_5_out, xor_1_out,
       xor_2_out, xor_3_out, xor_4_out;

  or or_1 (or_1_out, CPu, CPd);
  and and_1 (and_1_out, or_1_out, multiplexer_1_out);
  Multiplexer #(.select(1), .width(1), .disabled("Z"), .enable("false")) multiplexer_1 (
    .in0(QA), .in1(not_1_out), .out(multiplexer_1_out), .sel(CPd));
  Multiplexer #(.select(1), .width(1), .disabled("Z"), .enable("false")) multiplexer_2 (
    .in0(QB), .in1(not_2_out), .out(multiplexer_2_out), .sel(CPd));
  not not_1 (not_1_out, QA);
  Multiplexer #(.select(1), .width(1), .disabled("Z"), .enable("false")) multiplexer_3 (
    .in0(QC), .in1(not_3_out), .out(multiplexer_3_out), .sel(CPd));
  and and_2 (and_2_out, and_1_out, multiplexer_2_out);
  not not_2 (not_2_out, QB);
  and and_3 (and_3_out, and_2_out, multiplexer_3_out);
  not not_3 (not_3_out, QC);
  xor xor_1 (xor_1_out, QD, and_3_out);
  xor xor_2 (xor_2_out, and_2_out, QC);
  xor xor_3 (xor_3_out, QB, and_1_out);
  xor xor_4 (xor_4_out, or_1_out, QA);
  D_Flip_Flop #(.trigger("falling"), .Pre_Clr_Positions("LEGACY"), .NegatePresetClear("false"), .enable("false"), .NewFFLayout("true")) d_ff_1 (
    .clk(or_1_out), .D(xor_1_out), .Q(QD), .preset(and_4_out), .reset(or_5_out));  // open: Qn
  and and_4 (and_4_out, D, not_4_out);
  D_Flip_Flop #(.trigger("falling"), .Pre_Clr_Positions("LEGACY"), .NegatePresetClear("false"), .enable("false"), .NewFFLayout("true")) d_ff_2 (
    .clk(or_1_out), .D(xor_2_out), .Q(QC), .preset(and_5_out), .reset(or_2_out));  // open: Qn
  and and_5 (and_5_out, C, not_4_out);
  D_Flip_Flop #(.trigger("falling"), .Pre_Clr_Positions("LEGACY"), .NegatePresetClear("false"), .enable("false"), .NewFFLayout("true")) d_ff_3 (
    .clk(or_1_out), .D(xor_3_out), .Q(QB), .preset(and_6_out), .reset(or_3_out));  // open: Qn
  and and_6 (and_6_out, B, not_4_out);
  D_Flip_Flop #(.trigger("falling"), .Pre_Clr_Positions("LEGACY"), .NegatePresetClear("false"), .enable("false"), .NewFFLayout("true")) d_ff_4 (
    .clk(or_1_out), .D(xor_4_out), .Q(QA), .preset(and_7_out), .reset(or_4_out));  // open: Qn
  or or_2 (or_2_out, CLR, nor_1_out);
  or or_3 (or_3_out, CLR, nor_2_out);
  or or_4 (or_4_out, CLR, nor_3_out);
  and and_7 (and_7_out, A, not_4_out);
  or or_5 (or_5_out, CLR, nor_4_out);
  nor nor_1 (nor_1_out, LD, C);
  nor nor_2 (nor_2_out, LD, B);
  nor nor_3 (nor_3_out, LD, A);
  nor nor_4 (nor_4_out, LD, D);
  not not_4 (not_4_out, LD);
endmodule

module \六十进制计数器  (
  input  Adj,
  input  CPu,
  input  CPd,
  input  CLR,
  output Q1A,
  output Q1B,
  output Q1C,
  output Q1D,
  output Q0A,
  output Q0B,
  output Q0C,
  output Q0D,
  output out_13
);

  wire and_1_out, and_2_out, and_3_out, comparator_1_eq, comparator_2_eq, nor_1_out, not_1_out, not_2_out,
       or_1_out;
  wire [7:0] \四位二进制可逆计数器封装_1_out_4 ;
  wire [7:4] divider_1_out, divider_1_rem;

  Comparator #(.width(8), .mode("unsigned")) comparator_1 (
    .a({8{1'b0}}), .b(\四位二进制可逆计数器封装_1_out_4 ), .eq(comparator_1_eq));  // open: gt, lt
  or or_1 (or_1_out, CLR, comparator_2_eq);
  not not_1 (not_1_out, comparator_1_eq);
  and and_1 (and_1_out, Adj, CPd, not_1_out);
  \四位二进制可逆计数器封装  \u_四位二进制可逆计数器封装_1  (
    .in_1(CPu), .in_2(and_1_out), .in_3(or_1_out), .out_4(\四位二进制可逆计数器封装_1_out_4 [0]),
    .out_5(\四位二进制可逆计数器封装_1_out_4 [1]), .out_6(\四位二进制可逆计数器封装_1_out_4 [2]), .out_7(\四位二进制可逆计数器封装_1_out_4 [3]));
  not not_2 (not_2_out, Adj);
  nor nor_1 (nor_1_out, \四位二进制可逆计数器封装_1_out_4 [3], \四位二进制可逆计数器封装_1_out_4 [2], \四位二进制可逆计数器封装_1_out_4 [1], \四位二进制可逆计数器封装_1_out_4 [0]);
  and and_2 (and_2_out, CPu, \四位二进制可逆计数器封装_1_out_4 [0], \四位二进制可逆计数器封装_1_out_4 [1], \四位二进制可逆计数器封装_1_out_4 [2], \四位二进制可逆计数器封装_1_out_4 [3]);
  and and_3 (and_3_out, nor_1_out, and_1_out);
  \四位二进制可逆计数器封装  \u_四位二进制可逆计数器封装_2  (
    .in_1(and_2_out), .in_2(and_3_out), .in_3(or_1_out), .out_4(\四位二进制可逆计数器封装_1_out_4 [4]),
    .out_5(\四位二进制可逆计数器封装_1_out_4 [5]), .out_6(\四位二进制可逆计数器封装_1_out_4 [6]), .out_7(\四位二进制可逆计数器封装_1_out_4 [7]));
  Comparator #(.width(8), .mode("unsigned")) comparator_2 (
    .a(\四位二进制可逆计数器封装_1_out_4 ), .b(8'h3c), .eq(comparator_2_eq));  // open: gt, lt
  Divider #(.width(8)) divider_1 (
    .a(\四位二进制可逆计数器封装_1_out_4 ), .b(8'ha), .out({divider_1_out, Q1D, Q1C, Q1B, Q1A}),
    .rem({divider_1_rem, Q0D, Q0C, Q0B, Q0A}));  // open: upper
  nand nand_1 (out_13, comparator_2_eq, not_2_out);
endmodule

module \六十进制计数器测试电路  (
  input  in_1,
  input  in_2,
  output out_3
);

  wire button_1_out, button_2_out;
  wire [3:0] \六十进制计数器_1_q0a , \六十进制计数器_1_q1a ;

  Button button_1 (.out(button_1_out));
  Button button_2 (.out(button_2_out));
  \六十进制计数器  \u_六十进制计数器_1  (
    .Adj(in_1), .CPu(button_1_out), .CPd(button_2_out), .CLR(in_2), .Q1A(\六十进制计数器_1_q1a [0]),
    .Q1B(\六十进制计数器_1_q1a [1]), .Q1C(\六十进制计数器_1_q1a [2]), .Q1D(\六十进制计数器_1_q1a [3]), .Q0A(\六十进制计数器_1_q0a [0]),
    .Q0B(\六十进制计数器_1_q0a [1]), .Q0C(\六十进制计数器_1_q0a [2]), .Q0D(\六十进制计数器_1_q0a [3]), .out_13(out_3));
  Hex_Digit_Display hex_digit_display_1 (.value(\六十进制计数器_1_q1a ));  // open: dp
  Hex_Digit_Display hex_digit_display_2 (.value(\六十进制计数器_1_q0a ));  // open: dp
endmodule

module \十二进制计数器或二十四进制的计数器电路  (
  input  CPu,
  input  CPd,
  input  CLR,
  input  Adj,
  input  SET,
  output Q1D,
  output Q1C,
  output Q1B,
  output Q1A,
  output Q0D,
  output Q0C,
  output Q0B,
  output QCC,
  output Q0A
);

  wire and_1_out, and_2_out, and_4_out, comparator_1_eq, comparator_1_lt, comparator_2_gt, d_ff_1_q,
       d_ff_1_qn, not_1_out, not_2_out, not_3_out, or_1_out, or_2_out;
  wire [3:0] \四位二进制可逆计数器封装_1_out_4 ;
  wire [7:0] adder_1_out, multiplexer_1_out, multiplexer_2_out;
  wire [7:4] divider_1_out, divider_1_rem;

  and and_1 (and_1_out, CPd, comparator_2_gt);
  or or_1 (or_1_out, CLR, comparator_1_eq);
  \四位二进制可逆计数器封装  \u_四位二进制可逆计数器封装_1  (
    .in_1(CPu), .in_2(and_1_out), .in_3(or_1_out), .out_4(\四位二进制可逆计数器封装_1_out_4 [0]),
    .out_5(\四位二进制可逆计数器封装_1_out_4 [1]), .out_6(\四位二进制可逆计数器封装_1_out_4 [2]), .out_7(\四位二进制可逆计数器封装_1_out_4 [3]));
  not not_1 (not_1_out, Adj);
  Comparator #(.width(8), .mode("twosComplement")) comparator_1 (
    .a({4'b0000, \四位二进制可逆计数器封装_1_out_4 }), .b(8'hc), .eq(comparator_1_eq), .lt(comparator_1_lt));  // open: gt
  Comparator #(.width(8), .mode("unsigned")) comparator_2 (
    .a({4'b0000, \四位二进制可逆计数器封装_1_out_4 }), .b({8{1'b0}}), .gt(comparator_2_gt));  // open: eq, lt
  Adder #(.width(8)) adder_1 (.a({4'b0000, \四位二进制可逆计数器封装_1_out_4 }), .b(8'hc), .out(adder_1_out));  // open: cin, cout
  Multiplexer #(.select(1), .width(8), .disabled("Z"), .enable("false")) multiplexer_1 (
    .in0({4'b0000, \四位二进制可逆计数器封装_1_out_4 }), .in1(adder_1_out), .out(multiplexer_1_out), .sel(and_4_out));
  not not_2 (not_2_out, comparator_1_lt);
  or or_2 (or_2_out, not_1_out, SET);
  Multiplexer #(.select(1), .width(8), .disabled("Z"), .enable("false")) multiplexer_2 (
    .in0(multiplexer_1_out), .in1({4'b0000, \四位二进制可逆计数器封装_1_out_4 }), .out(multiplexer_2_out), .sel(and_2_out));
  and and_2 (and_2_out, not_2_out, not_3_out);
  and and_3 (QCC, comparator_1_eq, or_2_out);
  not not_3 (not_3_out, SET);
  and and_4 (and_4_out, d_ff_1_q, SET);
  D_Flip_Flop #(.trigger("rising"), .Pre_Clr_Positions("ABOVE_BELOW"), .NegatePresetClear("false"), .enable("false"), .NewFFLayout("true")) d_ff_1 (
    .clk(QCC), .D(d_ff_1_qn), .Q(d_ff_1_q), .Qn(d_ff_1_qn));  // open: preset, reset
  Divider #(.width(8)) divider_1 (
    .a(multiplexer_2_out), .b(8'ha), .out({divider_1_out, Q1D, Q1C, Q1B, Q1A}),
    .rem({divider_1_rem, Q0D, Q0C, Q0B, Q0A}));  // open: upper
endmodule

module \十二进制计数器或二十四进制的计数器测试电路  (
  input  in_1,
  input  in_2,
  input  in_3,
  output out_4
);

  wire button_1_out, button_2_out;
  wire [3:0] \十二进制计数器或二十四进制的计数器电路_1_q0a , \十二进制计数器或二十四进制的计数器电路_1_q1a ;

  Button button_1 (.out(button_1_out));
  Button button_2 (.out(button_2_out));
  \十二进制计数器或二十四进制的计数器电路  \u_十二进制计数器或二十四进制的计数器电路_1  (
    .Adj(in_1), .CPu(button_1_out), .CPd(button_2_out), .CLR(in_2), .QCC(out_4),
    .Q0D(\十二进制计数器或二十四进制的计数器电路_1_q0a [3]), .Q0C(\十二进制计数器或二十四进制的计数器电路_1_q0a [2]),
    .Q0B(\十二进制计数器或二十四进制的计数器电路_1_q0a [1]), .Q0A(\十二进制计数器或二十四进制的计数器电路_1_q0a [0]), .SET(in_3),
    .Q1D(\十二进制计数器或二十四进制的计数器电路_1_q1a [3]), .Q1C(\十二进制计数器或二十四进制的计数器电路_1_q1a [2]),
    .Q1B(\十二进制计数器或二十四进制的计数器电路_1_q1a [1]), .Q1A(\十二进制计数器或二十四进制的计数器电路_1_q1a [0]));
  Hex_Digit_Display hex_digit_display_1 (.value(\十二进制计数器或二十四进制的计数器电路_1_q1a ));  // open: dp
  Hex_Digit_Display hex_digit_display_2 (.value(\十二进制计数器或二十四进制的计数器电路_1_q0a ));  // open: dp
endmodule

module \上下午文字显示的电路  (
  input  AM_TM,
  input  TT,
  output [4:0] out_3,
  output [4:0] out_4,
  output [4:0] out_5,
  output [4:0] out_6
);

  wire not_1_out;

  and and_1 (out_3[0], not_1_out, TT);
  not not_1 (not_1_out, AM_TM);
  and and_2 (out_3[4], AM_TM, TT);

  assign out_3[3:1] = 3'b000;
  assign out_4 = {5{TT}};
  assign out_5 = {out_3[4], 1'b0, TT, 1'b0, out_3[0]};
  assign out_6 = {out_3[4], 3'b000, out_3[0]};
endmodule

module \上下午文字显示测试电路  (
  input  in_1,
  input  in_2
);

  wire [4:0] \上下午文字显示的电路_1_out_3 , \上下午文字显示的电路_1_out_4 , \上下午文字显示的电路_1_out_5 , \上下午文字显示的电路_1_out_6 ;

  DotMatrix #(.inputtype("column"), .matrixcols(4), .matrixrows(5), .persist(0), .dotshape("square")) dotmatrix_1 (
    .col0(\上下午文字显示的电路_1_out_3 ), .col1(\上下午文字显示的电路_1_out_4 ), .col2(\上下午文字显示的电路_1_out_5 ),
    .col3(\上下午文字显示的电路_1_out_6 ));
  \上下午文字显示的电路  \u_上下午文字显示的电路_1  (
    .out_3(\上下午文字显示的电路_1_out_3 ), .out_4(\上下午文字显示的电路_1_out_4 ), .out_5(\上下午文字显示的电路_1_out_5 ),
    .out_6(\上下午文字显示的电路_1_out_6 ), .AM_TM(in_1), .TT(in_2));
endmodule

module \电子钟整点报时电路  (
  input  [7:0] minute,
  input  [7:0] second,
  output led
);

  wire comparator_1_eq, comparator_2_gt;

  Comparator #(.width(8), .mode("twosComplement")) comparator_1 (
    .a(minute), .b(8'h3b), .eq(comparator_1_eq));  // open: gt, lt
  Comparator #(.width(8), .mode("twosComplement")) comparator_2 (
    .a(second), .b(8'h31), .gt(comparator_2_gt));  // open: eq, lt
  and and_1 (led, comparator_1_eq, comparator_2_gt);
endmodule

module \电子钟整点报时电路测试电路  (
  input  [7:0] in_1,
  input  [7:0] in_2
);

  wire \电子钟整点报时电路_1_led ;

  LED #(.active("true")) led_1 (.in(\电子钟整点报时电路_1_led ));
  \电子钟整点报时电路  \u_电子钟整点报时电路_1  (.minute(in_1), .second(in_2), .led(\电子钟整点报时电路_1_led ));
endmodule

module \秒脉冲产生电路  (
  input  in_1,
  output out_2
);

  wire d_ff_1_q, d_ff_1_qn, d_ff_2_q, d_ff_2_qn, d_ff_3_qn;

  D_Flip_Flop #(.trigger("rising"), .Pre_Clr_Positions("ABOVE_BELOW"), .NegatePresetClear("false"), .enable("false"), .NewFFLayout("true")) d_ff_1 (
    .clk(in_1), .D(d_ff_1_qn), .Q(d_ff_1_q), .Qn(d_ff_1_qn));  // open: preset, reset
  D_Flip_Flop #(.trigger("rising"), .Pre_Clr_Positions("ABOVE_BELOW"), .NegatePresetClear("false"), .enable("false"), .NewFFLayout("true")) d_ff_2 (
    .clk(d_ff_1_q), .D(d_ff_2_qn), .Q(d_ff_2_q), .Qn(d_ff_2_qn));  // open: preset, reset
  D_Flip_Flop #(.trigger("rising"), .Pre_Clr_Positions("ABOVE_BELOW"), .NegatePresetClear("false"), .enable("false"), .NewFFLayout("true")) d_ff_3 (
    .clk(d_ff_2_q), .D(d_ff_3_qn), .Q(out_2), .Qn(d_ff_3_qn));  // open: preset, reset
endmodule

module \多功能数字钟  (
  input  CPu,
  input  Adj0,
  input  _8hz,
  input  CLR,
  input  SET,
  input  CPd,
  input  Adj1,
  output [3:0] t1,
  output [3:0] m1,
  output [3:0] h1,
  output [3:0] h0,
  output [3:0] t0,
  output [3:0] m0,
  output [4:0] Q1,
  output [4:0] Q2,
  output [4:0] out_16,
  output [4:0] out_17,
  output out_18
);

  wire and_1_out, and_2_out, and_3_out, and_4_out, and_5_out, and_6_out, d_ff_1_q, d_ff_1_qn, not_1_out,
       not_2_out, not_3_out, not_4_out, not_5_out, not_6_out, or_1_out, or_2_out, \六十进制计数器_1_out_13 ,
       \六十进制计数器_2_out_13 , \十二进制计数器或二十四进制的计数器电路_1_qcc , \秒脉冲产生电路_1_out_2 ;
  wire [7:0] adder_1_out, adder_2_out, bit_extender_1_out, bit_extender_2_out, bit_extender_3_out,
       bit_extender_4_out, multiplier_1_out, multiplier_2_out;

  \秒脉冲产生电路  \u_秒脉冲产生电路_1  (.in_1(_8hz), .out_2(\秒脉冲产生电路_1_out_2 ));
  \六十进制计数器  \u_六十进制计数器_1  (
    .Adj(Adj0), .CPu(\秒脉冲产生电路_1_out_2 ), .CLR(CLR), .Q1A(t1[0]), .Q1B(t1[1]), .Q1C(t1[2]), .Q1D(t1[3]),
    .Q0A(t0[0]), .Q0B(t0[1]), .Q0C(t0[2]), .Q0D(t0[3]), .out_13(\六十进制计数器_1_out_13 ));  // open: CPd
  not not_1 (not_1_out, \六十进制计数器_1_out_13 );
  not not_2 (not_2_out, Adj0);
  and and_1 (and_1_out, CPu, Adj0, Adj1);
  and and_2 (and_2_out, not_2_out, not_1_out);
  assign bit_extender_1_out = {{4{1'b0}}, t0};  // Bit_Extender bit_extender_1
  assign bit_extender_2_out = {{4{1'b0}}, t1};  // Bit_Extender bit_extender_2
  or or_1 (or_1_out, and_1_out, and_2_out);
  Multiplier #(.width(8)) multiplier_1 (.a(bit_extender_2_out), .b(8'ha), .out(multiplier_1_out));  // open: cin, cout
  and and_3 (and_3_out, Adj0, CPd, Adj1);
  Adder #(.width(8)) adder_1 (.a(bit_extender_1_out), .b(multiplier_1_out), .out(adder_1_out));  // open: cin, cout
  \六十进制计数器  \u_六十进制计数器_2  (
    .Adj(Adj0), .CPu(or_1_out), .CPd(and_3_out), .CLR(CLR), .Q1A(m1[0]), .Q1B(m1[1]), .Q1C(m1[2]),
    .Q1D(m1[3]), .Q0A(m0[0]), .Q0B(m0[1]), .Q0C(m0[2]), .Q0D(m0[3]), .out_13(\六十进制计数器_2_out_13 ));
  not not_3 (not_3_out, Adj0);
  not not_4 (not_4_out, \六十进制计数器_2_out_13 );
  assign bit_extender_3_out = {{4{1'b0}}, m1};  // Bit_Extender bit_extender_3
  assign bit_extender_4_out = {{4{1'b0}}, m0};  // Bit_Extender bit_extender_4
  and and_4 (and_4_out, Adj0, CPu, not_5_out);
  and and_5 (and_5_out, not_3_out, not_4_out);
  or or_2 (or_2_out, and_4_out, and_5_out);
  not not_5 (not_5_out, Adj1);
  Multiplier #(.width(8)) multiplier_2 (.a(bit_extender_3_out), .b(8'ha), .out(multiplier_2_out));  // open: cin, cout
  and and_6 (and_6_out, Adj0, CPd, not_5_out);
  Adder #(.width(8)) adder_2 (.a(multiplier_2_out), .b(bit_extender_4_out), .out(adder_2_out));  // open: cin, cout
  \十二进制计数器或二十四进制的计数器电路  \u_十二进制计数器或二十四进制的计数器电路_1  (
    .Adj(Adj0), .CPu(or_2_out), .CPd(and_6_out), .CLR(CLR), .QCC(\十二进制计数器或二十四进制的计数器电路_1_qcc ), .Q0D(h0[3]),
    .Q0C(h0[2]), .Q0B(h0[1]), .Q0A(h0[0]), .SET(SET), .Q1D(h1[3]), .Q1C(h1[2]), .Q1B(h1[1]), .Q1A(h1[0]));
  not not_6 (not_6_out, SET);
  \电子钟整点报时电路  \u_电子钟整点报时电路_1  (.minute(adder_2_out), .second(adder_1_out), .led(out_18));
  D_Flip_Flop #(.trigger("rising"), .Pre_Clr_Positions("ABOVE_BELOW"), .NegatePresetClear("false"), .enable("false"), .NewFFLayout("true")) d_ff_1 (
    .clk(\十二进制计数器或二十四进制的计数器电路_1_qcc ), .D(d_ff_1_qn), .Q(d_ff_1_q), .Qn(d_ff_1_qn));  // open: preset, reset
  \上下午文字显示的电路  \u_上下午文字显示的电路_1  (
    .out_3(Q1), .out_4(Q2), .out_5(out_16), .out_6(out_17), .AM_TM(d_ff_1_q), .TT(not_6_out));
endmodule

module \多功能数字钟测试电路  (
  input  in_1,
  input  in_2,
  input  in_3,
  input  in_4
);

  wire button_1_out, button_2_out, clock_1_out, \多功能数字钟_1_out_18 ;
  wire [3:0] \多功能数字钟_1_h0 , \多功能数字钟_1_h1 , \多功能数字钟_1_m0 , \多功能数字钟_1_m1 , \多功能数字钟_1_t0 , \多功能数字钟_1_t1 ;
  wire [4:0] \多功能数字钟_1_out_16 , \多功能数字钟_1_out_17 , \多功能数字钟_1_q1 , \多功能数字钟_1_q2 ;

  DotMatrix #(.inputtype("column"), .matrixcols(4), .matrixrows(5), .persist(0), .dotshape("square")) dotmatrix_1 (
    .col0(\多功能数字钟_1_q1 ), .col1(\多功能数字钟_1_q2 ), .col2(\多功能数字钟_1_out_16 ), .col3(\多功能数字钟_1_out_17 ));
  \多功能数字钟  \u_多功能数字钟_1  (
    ._8hz(clock_1_out), .t1(\多功能数字钟_1_t1 ), .m1(\多功能数字钟_1_m1 ), .t0(\多功能数字钟_1_t0 ), .m0(\多功能数字钟_1_m0 ),
    .Q1(\多功能数字钟_1_q1 ), .Q2(\多功能数字钟_1_q2 ), .out_16(\多功能数字钟_1_out_16 ), .out_17(\多功能数字钟_1_out_17 ),
    .CPu(button_1_out), .Adj0(in_1), .CLR(in_4), .CPd(button_2_out), .Adj1(in_2), .SET(in_3),
    .out_18(\多功能数字钟_1_out_18 ), .h1(\多功能数字钟_1_h1 ), .h0(\多功能数字钟_1_h0 ));
  Button button_1 (.out(button_1_out));
  Clock #(.highDuration(1), .lowDuration(1)) clock_1 (.out(clock_1_out));
  Hex_Digit_Display hex_digit_display_1 (.value(\多功能数字钟_1_h1 ));  // open: dp
  Hex_Digit_Display hex_digit_display_2 (.value(\多功能数字钟_1_h0 ));  // open: dp
  Button button_2 (.out(button_2_out));
  Hex_Digit_Display hex_digit_display_3 (.value(\多功能数字钟_1_m1 ));  // open: dp
  Hex_Digit_Display hex_digit_display_4 (.value(\多功能数字钟_1_m0 ));  // open: dp
  Hex_Digit_Display hex_digit_display_5 (.value(\多功能数字钟_1_t1 ));  // open: dp
  LED #(.active("true")) led_1 (.in(\多功能数字钟_1_out_18 ));
  Hex_Digit_Display hex_digit_display_6 (.value(\多功能数字钟_1_t0 ));  // open: dp
endmodule

module \四位二进制可逆计数器封装  (
  input  in_1,
  input  in_2,
  input  in_3,
  output out_4,
  output out_5,
  output out_6,
  output out_7
);

  \四位二进制可逆计数器  \u_四位二进制可逆计数器_1  (
    .CPu(in_1), .CPd(in_2), .QD(out_7), .D(1'b0), .QC(out_6), .C(1'b0), .LD(1'b1), .QB(out_5), .B(1'b0),
    .CLR(in_3), .QA(out_4), .A(1'b0));
endmodule

module \_12_24转换电路  (
);

  \十二进制计数器或二十四进制的计数器电路  \u_十二进制计数器或二十四进制的计数器电路_1  ();  // open: Adj, CPu, CPd, CLR, QCC, Q0D, Q0C, Q0B, Q0A, SET, Q1D, Q1C, Q1B, Q1A
endmodule

module \秒脉冲产生电路测试  (
  input  in_1,
  output out_2
);

  \秒脉冲产生电路  \u_秒脉冲产生电路_1  (.in_1(in_1), .out_2(out_2));
endmodule
