// Logisim project 实验6.circ as structural Verilog: 7 circuits, main circuit sqrX
// sqrx
module sqrX (
  input  [31:0] A,
  input  [31:0] B,
  input  [31:0] C,
  input  [31:0] D,
  output [31:0] AA,
  output [31:0] BB,
  output [31:0] CC,
  output [31:0] DD
);

  wire [31:0] multiplier_1_out, multiplier_2_out, multiplier_3_out, multiplier_4_out, multiplier_5_out,
       multiplier_6_out, multiplier_7_out;

  Multiplier #(.width(32)) multiplier_1 (.a(A), .b(A), .out(multiplier_1_out));  // open: cin, cout
  Multiplier #(.width(32)) multiplier_2 (.a(A), .b(B), .out(multiplier_2_out));  // open: cin, cout
  Multiplier #(.width(32)) multiplier_3 (.a(B), .b(C), .out(multiplier_3_out));  // open: cin, cout
  Multiplier #(.width(32)) multiplier_4 (.a(C), .b(A), .out(multiplier_4_out));  // open: cin, cout
  Multiplier #(.width(32)) multiplier_5 (.a(B), .b(D), .out(multiplier_5_out));  // open: cin, cout
  Multiplier #(.width(32)) multiplier_6 (.a(D), .b(C), .out(multiplier_6_out));  // open: cin, cout
  Multiplier #(.width(32)) multiplier_7 (.a(D), .b(D), .out(multiplier_7_out));  // open: cin, cout
  Adder #(.width(32)) adder_1 (.a(multiplier_1_out), .b(multiplier_3_out), .out(AA));  // open: cin, cout
  Adder #(.width(32)) adder_2 (.a(multiplier_2_out), .b(multiplier_5_out), .out(BB));  // open: cin, cout
  Adder #(.width(32)) adder_3 (.a(multiplier_4_out), .b(multiplier_6_out), .out(CC));  // open: cin, cout
  Adder #(.width(32)) adder_4 (.a(multiplier_3_out), .b(multiplier_7_out), .out(DD));  // open: cin, cout
endmodule

// sqrx*A
module sqrX_A (
  input  [31:0] A,
  input  [31:0] B,
  input  [31:0] C,
  input  [31:0] D,
  output [31:0] QA,
  output [31:0] QB,
  output [31:0] QC,
  output [31:0] QD
);

  wire [31:0] adder_3_out, adder_5_out, multiplier_1_out, multiplier_2_out, multiplier_3_out,
       multiplier_4_out, multiplier_5_out, multiplier_6_out, multiplier_7_out;

  Multiplier #(.width(32)) multiplier_1 (.a(A), .b(A), .out(multiplier_1_out));  // open: cin, cout
  Multiplier #(.width(32)) multiplier_2 (.a(B), .b(A), .out(multiplier_2_out));  // open: cin, cout
  Multiplier #(.width(32)) multiplier_3 (.a(B), .b(C), .out(multiplier_3_out));  // open: cin, cout
  Multiplier #(.width(32)) multiplier_4 (.a(C), .b(A), .out(multiplier_4_out));  // open: cin, cout
  Multiplier #(.width(32)) multiplier_5 (.a(D), .b(B), .out(multiplier_5_out));  // open: cin, cout
  Multiplier #(.width(32)) multiplier_6 (.a(C), .b(D), .out(multiplier_6_out));  // open: cin, cout
  Multiplier #(.width(32)) multiplier_7 (.a(D), .b(D), .out(multiplier_7_out));  // open: cin, cout
  Adder #(.width(32)) adder_1 (.a(multiplier_2_out), .b(multiplier_5_out), .out(QA));  // open: cin, cout
  Adder #(.width(32)) adder_2 (.a(multiplier_3_out), .b(multiplier_7_out), .out(QC));  // open: cin, cout
  Adder #(.width(32)) adder_3 (.a(QA), .b(multiplier_1_out), .out(adder_3_out));  // open: cin, cout
  Adder #(.width(32)) adder_4 (.a(adder_3_out), .b(multiplier_3_out), .out(QB));  // open: cin, cout
  Adder #(.width(32)) adder_5 (.a(QC), .b(multiplier_4_out), .out(adder_5_out));  // open: cin, cout
  Adder #(.width(32)) adder_6 (.a(adder_5_out), .b(multiplier_6_out), .out(QD));  // open: cin, cout
endmodule

module \Fibonacci数显示模块  (
  input  [31:0] FIB,
  output [3:0] D0,
  output [3:0] D1,
  output [3:0] D2,
  output [3:0] D3,
  output [3:0] D4,
  output [3:0] D5,
  output [3:0] D6,
  output [3:0] D7,
  output [3:0] D8,
  output [3:0] D9
);

  wire [3:0] divider_6_rem, divider_6_rem_2, divider_6_rem_3, divider_6_rem_4, divider_6_rem_5,
       divider_6_rem_6;
  wire [31:0] divider_1_out, divider_2_out, divider_3_out, divider_4_out, divider_5_out, divider_6_out,
       divider_7_out, divider_8_out;
  wire [31:4] divider_1_rem, divider_2_rem, divider_3_rem, divider_4_rem, divider_5_rem, divider_7_rem,
       divider_8_rem, divider_9_out, divider_9_rem;
  wire [31:28] divider_6_rem_7;

  Divider #(.width(32)) divider_1 (.a(FIB), .b(32'ha), .out(divider_1_out), .rem({divider_1_rem, D0}));  // open: upper
  Divider #(.width(32)) divider_2 (
    .a(divider_1_out), .b(32'ha), .out(divider_2_out), .rem({divider_2_rem, D1}));  // open: upper
  Divider #(.width(32)) divider_3 (
    .a(divider_2_out), .b(32'ha), .out(divider_3_out), .rem({divider_3_rem, D2}));  // open: upper
  Divider #(.width(32)) divider_4 (
    .a(divider_3_out), .b(32'ha), .out(divider_4_out), .rem({divider_4_rem, D3}));  // open: upper
  Divider #(.width(32)) divider_5 (
    .a(divider_4_out), .b(32'ha), .out(divider_5_out), .rem({divider_5_rem, D4}));  // open: upper
  Divider #(.width(32)) divider_6 (
    .a(divider_5_out), .b(32'ha), .out(divider_6_out),
    .rem({divider_6_rem_7, divider_6_rem_6, divider_6_rem_5, divider_6_rem_4, divider_6_rem_3, divider_6_rem_2, divider_6_rem, D5}));  // open: upper
  Divider #(.width(32)) divider_7 (
    .a(divider_6_out), .b(32'ha), .out(divider_7_out), .rem({divider_7_rem, D6}));  // open: upper
  Divider #(.width(32)) divider_8 (
    .a(divider_7_out), .b(32'ha), .out(divider_8_out), .rem({divider_8_rem, D7}));  // open: upper
  Divider #(.width(32)) divider_9 (
    .a(divider_8_out), .b(32'ha), .out({divider_9_out, D9}), .rem({divider_9_rem, D8}));  // open: upper
endmodule

module \斐波那契_Fibonacci_数列计算器  (
  input  START,
  input  CLR,
  input  Ni_1,
  input  CLK,
  output [31:0] FIB
);

  wire and_1_out, not_1_out;
  wire [31:0] enb_1_qa, enb_1_qb, enb_1_qc, enb_1_qd, multiplexer_1_out, multiplexer_2_out,
       multiplexer_3_out, multiplexer_4_out, multiplexer_6_out, multiplexer_7_out, multiplexer_8_out,
       multiplexer_9_out, sqrx_1_aa, sqrx_1_bb, sqrx_1_cc, sqrx_1_dd, sqrx_a_1_qa, sqrx_a_1_qb, sqrx_a_1_qc,
       sqrx_a_1_qd;

  not not_1 (not_1_out, CLR);
  and and_1 (and_1_out, START, not_1_out);
  Multiplexer #(.select(1), .width(32), .disabled("Z"), .enable("false")) multiplexer_1 (
    .in0({32{1'b0}}), .in1(multiplexer_6_out), .out(multiplexer_1_out), .sel(and_1_out));
  Multiplexer #(.select(1), .width(32), .disabled("Z"), .enable("false")) multiplexer_2 (
    .in0(32'h1), .in1(multiplexer_7_out), .out(multiplexer_2_out), .sel(and_1_out));
  Multiplexer #(.select(1), .width(32), .disabled("Z"), .enable("false")) multiplexer_3 (
    .in0(32'h1), .in1(multiplexer_8_out), .out(multiplexer_3_out), .sel(and_1_out));
  Multiplexer #(.select(1), .width(32), .disabled("Z"), .enable("false")) multiplexer_4 (
    .in0(32'h1), .in1(multiplexer_9_out), .out(multiplexer_4_out), .sel(and_1_out));
  ENB enb_1 (
    .A(multiplexer_1_out), .B(multiplexer_2_out), .C(multiplexer_3_out), .D(multiplexer_4_out), .CLK(CLK),
    .CLR(CLR), .QA(enb_1_qa), .QB(enb_1_qb), .QC(enb_1_qc), .QD(enb_1_qd));
  Multiplexer #(.select(1), .width(32), .disabled("Z"), .enable("false")) multiplexer_5 (
    .in0({32{1'b0}}), .in1(enb_1_qb), .out(FIB), .sel(and_1_out));
  sqrX sqrx_1 (
    .A(enb_1_qa), .B(enb_1_qb), .C(enb_1_qc), .D(enb_1_qd), .AA(sqrx_1_aa), .BB(sqrx_1_bb), .CC(sqrx_1_cc),
    .DD(sqrx_1_dd));
  sqrX_A sqrx_a_1 (
    .A(enb_1_qa), .B(enb_1_qb), .C(enb_1_qc), .D(enb_1_qd), .QA(sqrx_a_1_qa), .QB(sqrx_a_1_qb),
    .QC(sqrx_a_1_qc), .QD(sqrx_a_1_qd));
  Multiplexer #(.select(1), .width(32), .disabled("Z"), .enable("false")) multiplexer_6 (
    .in0(sqrx_1_aa), .in1(sqrx_a_1_qa), .out(multiplexer_6_out), .sel(Ni_1));
  Multiplexer #(.select(1), .width(32), .disabled("Z"), .enable("false")) multiplexer_7 (
    .in0(sqrx_1_bb), .in1(sqrx_a_1_qb), .out(multiplexer_7_out), .sel(Ni_1));
  Multiplexer #(.select(1), .width(32), .disabled("Z"), .enable("false")) multiplexer_8 (
    .in0(sqrx_1_cc), .in1(sqrx_a_1_qc), .out(multiplexer_8_out), .sel(Ni_1));
  Multiplexer #(.select(1), .width(32), .disabled("Z"), .enable("false")) multiplexer_9 (
    .in0(sqrx_1_dd), .in1(sqrx_a_1_qd), .out(multiplexer_9_out), .sel(Ni_1));
endmodule

module ENB (
  input  [31:0] A,
  input  [31:0] B,
  input  [31:0] C,
  input  [31:0] D,
  input  CLK,
  input  CLR,
  output [31:0] QA,
  output [31:0] QB,
  output [31:0] QC,
  output [31:0] QD
);

  Register #(.width(32), .trigger("rising"), .Select("low")) register_1 (
    .D(A), .Q(QA), .clk(CLK), .clr(CLR));  // open: en
  Register #(.width(32), .trigger("rising"), .Select("low")) register_2 (
    .D(B), .Q(QB), .clk(CLK), .clr(CLR));  // open: en
  Register #(.width(32), .trigger("rising"), .Select("low")) register_3 (
    .D(C), .Q(QC), .clk(CLK), .clr(CLR));  // open: en
  Register #(.width(32), .trigger("rising"), .Select("low")) register_4 (
    .D(D), .Q(QD), .clk(CLK), .clr(CLR));  // open: en
endmodule

module CONTROLLER (
  input  [5:0] n,
  input  CLR,
  input  CLK,
  output START,
  output CLR_2,
  output Ni_1,
  output CLK_2
);

  wire comparator_1_lt, or_1_out, or_2_out;
  wire [7:0] counter_1_q;

  Counter #(.width(8), .max('hff), .ongoal("wrap"), .trigger("rising"), .behavior("new")) counter_1 (
    .Q(counter_1_q), .clk(CLK), .clr(CLR));  // open: load, D, count, carry, preset, down
  Shift_Register #(.width(1), .length(6), .parallel("true"), .trigger("rising")) shift_register_1 (
    .shift(1'b1), .in(1'b0), .clk(or_1_out), .out(Ni_1), .load(CLR), .d0(n[0]), .d1(n[1]), .d2(n[2]),
    .d3(n[3]), .d4(n[4]), .d5(n[5]));  // open: clr, q0, q1, q2, q3, q4, q5
  Comparator #(.width(8), .mode("twosComplement")) comparator_1 (
    .a(counter_1_q), .b(8'h6), .lt(comparator_1_lt));  // open: gt, eq
  or or_1 (or_1_out, CLR, CLK_2);
  and and_1 (CLK_2, comparator_1_lt, CLK);
  or or_2 (or_2_out, START, Ni_1);
  Register #(.width(1), .trigger("rising"), .Select("low")) register_1 (
    .D(or_2_out), .Q(START), .clk(CLK_2), .clr(CLR));  // open: en

  assign CLR_2 = CLR;
endmodule

module \FIB总电路  (
  input  [5:0] in_1
);

  wire button_1_out, button_2_out, controller_1_clk_2, controller_1_clr_2, controller_1_ni_1,
       controller_1_start;
  wire [3:0] \fibonacci数显示模块_1_d0 , \fibonacci数显示模块_1_d1 , \fibonacci数显示模块_1_d2 , \fibonacci数显示模块_1_d3 ,
       \fibonacci数显示模块_1_d4 , \fibonacci数显示模块_1_d5 , \fibonacci数显示模块_1_d6 , \fibonacci数显示模块_1_d7 ,
       \fibonacci数显示模块_1_d8 , \fibonacci数显示模块_1_d9 ;
  wire [31:0] \斐波那契_fibonacci_数列计算器_1_fib ;

  Button button_1 (.out(button_1_out));
  Button button_2 (.out(button_2_out));
  CONTROLLER controller_1 (
    .n(in_1), .CLR(button_1_out), .CLK(button_2_out), .START(controller_1_start), .CLR_2(controller_1_clr_2),
    .Ni_1(controller_1_ni_1), .CLK_2(controller_1_clk_2));
  \斐波那契_Fibonacci_数列计算器  \u_斐波那契_fibonacci_数列计算器_1  (
    .START(controller_1_start), .CLR(controller_1_clr_2), .Ni_1(controller_1_ni_1), .CLK(controller_1_clk_2),
    .FIB(\斐波那契_fibonacci_数列计算器_1_fib ));
  \Fibonacci数显示模块  \fibonacci数显示模块_1  (
    .FIB(\斐波那契_fibonacci_数列计算器_1_fib ), .D0(\fibonacci数显示模块_1_d0 ), .D1(\fibonacci数显示模块_1_d1 ),
    .D2(\fibonacci数显示模块_1_d2 ), .D3(\fibonacci数显示模块_1_d3 ), .D4(\fibonacci数显示模块_1_d4 ),
    .D5(\fibonacci数显示模块_1_d5 ), .D6(\fibonacci数显示模块_1_d6 ), .D7(\fibonacci数显示模块_1_d7 ),
    .D8(\fibonacci数显示模块_1_d8 ), .D9(\fibonacci数显示模块_1_d9 ));
  Hex_Digit_Display hex_digit_display_1 (.value(\fibonacci数显示模块_1_d9 ));  // open: dp
  Hex_Digit_Display hex_digit_display_2 (.value(\fibonacci数显示模块_1_d8 ));  // open: dp
  Hex_Digit_Display hex_digit_display_3 (.value(\fibonacci数显示模块_1_d7 ));  // open: dp
  Hex_Digit_Display hex_digit_display_4 (.value(\fibonacci数显示模块_1_d5 ));  // open: dp
  Hex_Digit_Display hex_digit_display_5 (.value(\fibonacci数显示模块_1_d6 ));  // open: dp
  Hex_Digit_Display hex_digit_display_6 (.value(\fibonacci数显示模块_1_d4 ));  // open: dp
  Hex_Digit_Display hex_digit_display_7 (.value(\fibonacci数显示模块_1_d2 ));  // open: dp
  Hex_Digit_Display hex_digit_display_8 (.value(\fibonacci数显示模块_1_d3 ));  // open: dp
  Hex_Digit_Display hex_digit_display_9 (.value(\fibonacci数显示模块_1_d1 ));  // open: dp
  Hex_Digit_Display hex_digit_display_10 (.value(\fibonacci数显示模块_1_d0 ));  // open: dp
endmodule
