// Logisim project 门禁系统.circ as structural Verilog: 10 circuits, main circuit 四位二进制可逆计数器
// 可逆计数器
module \四位二进制可逆计数器  (
  input  D,
  input  CPu,
  input  C,
  input  LD,
  input  CPd,
  input  B,
  input  CLR,
  input  A,
  output QD,
  output QC,
  output QB,
  output QA
);

  wire and_1_out, and_2_out, and_3_out, and_4_out, and_5_out, and_6_out, and_7_out, multiplexer_1_out,
       multiplexer_2_out, multiplexer_3_out, nor_1_out, nor_2_out, nor_3_out, nor_4_out, not_1_out,
       not_2_out, not_3_out, not_4_out, or_1_out, or_2_out, or_3_out, or_4_out, or_5_out, xor_1_out,
       xor_2_out, xor_3_out, xor_4_out;

  or or_1 (or_1_out, CPu, CPd);
  and and_1 (and_1_out, or_1_out, multiplexer_1_out);
  Multiplexer #(.select(1), .width(1), .disabled("Z"), .enable("false")) multiplexer_1 (
    .in0(QA), .in1(not_1_out), .out(multiplexer_1_out), .sel(CPd));
  and and_2 (and_2_out, and_1_out, multiplexer_2_out);
  Multiplexer #(.select(1), .width(1), .disabled("Z"), .enable("false")) multiplexer_2 (
    .in0(QB), .in1(not_2_out), .out(multiplexer_2_out), .sel(CPd));
  not not_1 (not_1_out, QA);
  and and_3 (and_3_out, and_2_out, multiplexer_3_out);
  Multiplexer #(.select(1), .width(1), .disabled("Z"), .enable("false")) multiplexer_3 (
    .in0(QC), .in1(not_3_out), .out(multiplexer_3_out), .sel(CPd));
  not not_2 (not_2_out, QB);
  not not_3 (not_3_out, QC);
  xor xor_1 (xor_1_out, or_1_out, QA);
  xor xor_2 (xor_2_out, QD, and_3_out);
  xor xor_3 (xor_3_out, and_2_out, QC);
  xor xor_4 (xor_4_out, QB, and_1_out);
  D_Flip_Flop #(.trigger("falling"), .Pre_Clr_Positions("LEGACY"), .NegatePresetClear("false"), .enable("false"), .NewFFLayout("true")) d_ff_1 (
    .clk(or_1_out), .D(xor_2_out), .Q(QD), .preset(and_4_out), .reset(or_5_out));  // open: Qn
  and and_4 (and_4_out, D, not_4_out);
  D_Flip_Flop #(.trigger("falling"), .Pre_Clr_Positions("LEGACY"), .NegatePresetClear("false"), .enable("false"), .NewFFLayout("true")) d_ff_2 (
    .clk(or_1_out), .D(xor_3_out), .Q(QC), .preset(and_5_out), .reset(or_2_out));  // open: Qn
  and and_5 (and_5_out, C, not_4_out);
  D_Flip_Flop #(.trigger("falling"), .Pre_Clr_Positions("LEGACY"), .NegatePresetClear("false"), .enable("false"), .NewFFLayout("true")) d_ff_3 (
    .clk(or_1_out), .D(xor_4_out), .Q(QB), .preset(and_6_out), .reset(or_3_out));  // open: Qn
  and and_6 (and_6_out, B, not_4_out);
  D_Flip_Flop #(.trigger("falling"), .Pre_Clr_Positions("LEGACY"), .NegatePresetClear("false"), .enable("false"), .NewFFLayout("true")) d_ff_4 (
    .clk(or_1_out), .D(xor_1_out), .Q(QA), .preset(and_7_out), .reset(or_4_out));  // open: Qn
  and and_7 (and_7_out, A, not_4_out);
  or or_2 (or_2_out, CLR, nor_1_out);
  or or_3 (or_3_out, CLR, nor_2_out);
  or or_4 (or_4_out, CLR, nor_3_out);
  or or_5 (or_5_out, CLR, nor_4_out);
  nor nor_1 (nor_1_out, LD, C);
  nor nor_2 (nor_2_out, LD, B);
  nor nor_3 (nor_3_out, LD, A);
  nor nor_4 (nor_4_out, LD, D);
  not not_4 (not_4_out, LD);
endmodule

module \四位二进制可逆计数器测试电路  (
  input  CPu,
  input  CPd,
  input  CLR,
  input  D,
  input  C,
  input  B,
  input  A,
  input  LD,
  output QD,
  output QC,
  output QB,
  output QA
);

  \四位二进制可逆计数器  \u_四位二进制可逆计数器_1  (
    .CPu(CPu), .CPd(CPd), .QD(QD), .D(D), .QC(QC), .C(C), .LD(LD), .QB(QB), .B(B), .CLR(CLR), .QA(QA), .A(A));
endmodule

// 二进制转8421码
module \二进制转8421码电路  (
  input  A0,
  input  A1,
  input  A2,
  input  A3,
  output B0,
  output B1,
  output B2,
  output B3,
  output B7,
  output B6,
  output B5,
  output B4
);

  wire or_1_out;

  or or_1 (or_1_out, A1, A2);
  and and_1 (B4, or_1_out, A3);
  \先行进位的并行加法器  \u_先行进位的并行加法器_1  (
    .A0(A0), .B0(1'b0), .A1(A1), .B1(B4), .A2(A2), .B2(B4), .A3(A3), .B3(1'b0), .S0(B0), .S1(B1), .S2(B2),
    .S3(B3), .C0(1'b0));  // open: C4

  assign B5 = 1'b0;
  assign B6 = 1'b0;
  assign B7 = 1'b0;
endmodule

module \二进制转8421码测试电路  (
  input  A3,
  input  A2,
  input  A1,
  input  A0,
  output B7,
  output B6,
  output B5,
  output B4,
  output B3,
  output B2,
  output B1,
  output B0
);

  \二进制转8421码电路  \u_二进制转8421码电路_1  (
    .A0(A0), .A1(A1), .A2(A2), .A3(A3), .B0(B0), .B1(B1), .B2(B2), .B3(B3), .B7(B7), .B6(B6), .B5(B5), .B4(B4));
endmodule

module \显示电路  (
  input  A3,
  input  A2,
  input  A1,
  input  A0,
  input  B3,
  input  B2,
  input  B1,
  input  B0
);

  wire \n7段译码器_1_fa , \n7段译码器_1_fb , \n7段译码器_1_fc , \n7段译码器_1_fd , \n7段译码器_1_fe , \n7段译码器_1_ff ,
       \n7段译码器_1_fg , \n7段译码器_2_fa , \n7段译码器_2_fb , \n7段译码器_2_fc , \n7段译码器_2_fd , \n7段译码器_2_fe ,
       \n7段译码器_2_ff , \n7段译码器_2_fg ;

  \_7段译码器  \u_7段译码器_1  (
    .A3(A3), .A2(A2), .A1(A1), .A0(A0), .FA(\n7段译码器_1_fa ), .FB(\n7段译码器_1_fb ), .FC(\n7段译码器_1_fc ),
    .FD(\n7段译码器_1_fd ), .FE(\n7段译码器_1_fe ), .FF(\n7段译码器_1_ff ), .FG(\n7段译码器_1_fg ));
  \_7段译码器  \u_7段译码器_2  (
    .A3(B3), .A2(B2), .A1(B1), .A0(B0), .FA(\n7段译码器_2_fa ), .FB(\n7段译码器_2_fb ), .FC(\n7段译码器_2_fc ),
    .FD(\n7段译码器_2_fd ), .FE(\n7段译码器_2_fe ), .FF(\n7段译码器_2_ff ), .FG(\n7段译码器_2_fg ));
  _7_Segment_Display #(.active("true")) u_7_segment_display_1 (
    .g(\n7段译码器_1_fg ), .f(\n7段译码器_1_ff ), .a(\n7段译码器_1_fa ), .b(\n7段译码器_1_fb ), .e(\n7段译码器_1_fe ),
    .d(\n7段译码器_1_fd ), .c(\n7段译码器_1_fc ));  // open: dp
  _7_Segment_Display #(.active("true")) u_7_segment_display_2 (
    .g(\n7段译码器_2_fg ), .f(\n7段译码器_2_ff ), .a(\n7段译码器_2_fa ), .b(\n7段译码器_2_fb ), .e(\n7段译码器_2_fe ),
    .d(\n7段译码器_2_fd ), .c(\n7段译码器_2_fc ));  // open: dp
endmodule

// 可逆计数器报警电路
module \报警电路  (
  input  CPu,
  input  CPd,
  input  CLR,
  output ERROR,
  output QD,
  output QC,
  output QB,
  output QA
);

  wire and_2_out, multiplexer_1_out, multiplexer_2_out, or_1_out;

  Multiplexer #(.select(1), .width(1), .disabled("Z"), .enable("false")) multiplexer_1 (
    .in0(CPu), .in1(1'b0), .out(multiplexer_1_out), .sel(and_2_out));
  Multiplexer #(.select(1), .width(1), .disabled("Z"), .enable("false")) multiplexer_2 (
    .in0(1'b0), .in1(CPd), .out(multiplexer_2_out), .sel(or_1_out));
  and and_1 (ERROR, CPu, and_2_out);
  and and_2 (and_2_out, QA, QB, QC, QD);
  or or_1 (or_1_out, QD, QC, QB, QA);
  \四位二进制可逆计数器  \u_四位二进制可逆计数器_1  (
    .CPu(multiplexer_1_out), .CPd(multiplexer_2_out), .QD(QD), .D(1'b0), .QC(QC), .C(1'b0), .LD(1'b1),
    .QB(QB), .B(1'b0), .CLR(CLR), .QA(QA), .A(1'b0));
endmodule

module \小型实验室门禁系统  (
  input  CPu,
  input  CPd,
  input  CLR,
  output ERROR,
  output out_5,
  output out_6,
  output out_7,
  output out_8,
  output out_9,
  output out_10,
  output out_11,
  output out_12,
  output out_13,
  output out_14,
  output out_15,
  output out_16,
  output out_17,
  output out_18
);

  wire \二进制转8421码电路_1_b0 , \二进制转8421码电路_1_b1 , \二进制转8421码电路_1_b2 , \二进制转8421码电路_1_b3 , \二进制转8421码电路_1_b4 ,
       \二进制转8421码电路_1_b5 , \二进制转8421码电路_1_b6 , \二进制转8421码电路_1_b7 , \报警电路_1_qa , \报警电路_1_qb , \报警电路_1_qc ,
       \报警电路_1_qd ;

  \报警电路  \u_报警电路_1  (
    .CPu(CPu), .CPd(CPd), .CLR(CLR), .ERROR(ERROR), .QD(\报警电路_1_qd ), .QC(\报警电路_1_qc ), .QB(\报警电路_1_qb ),
    .QA(\报警电路_1_qa ));
  \二进制转8421码电路  \u_二进制转8421码电路_1  (
    .A0(\报警电路_1_qa ), .A1(\报警电路_1_qb ), .A2(\报警电路_1_qc ), .A3(\报警电路_1_qd ), .B0(\二进制转8421码电路_1_b0 ),
    .B1(\二进制转8421码电路_1_b1 ), .B2(\二进制转8421码电路_1_b2 ), .B3(\二进制转8421码电路_1_b3 ), .B7(\二进制转8421码电路_1_b7 ),
    .B6(\二进制转8421码电路_1_b6 ), .B5(\二进制转8421码电路_1_b5 ), .B4(\二进制转8421码电路_1_b4 ));
  \_7段译码器  \u_7段译码器_1  (
    .A3(\二进制转8421码电路_1_b7 ), .A2(\二进制转8421码电路_1_b6 ), .A1(\二进制转8421码电路_1_b5 ), .A0(\二进制转8421码电路_1_b4 ),
    .FA(out_5), .FB(out_6), .FC(out_7), .FD(out_8), .FE(out_9), .FF(out_10), .FG(out_11));
  \_7段译码器  \u_7段译码器_2  (
    .A3(\二进制转8421码电路_1_b3 ), .A2(\二进制转8421码电路_1_b2 ), .A1(\二进制转8421码电路_1_b1 ), .A0(\二进制转8421码电路_1_b0 ),
    .FA(out_12), .FB(out_13), .FC(out_14), .FD(out_15), .FE(out_16), .FF(out_17), .FG(out_18));
endmodule

module \小型门禁系统测试电路  (
  input  CPu,
  input  CPd,
  input  CLR,
  output ERROR
);

  wire \小型实验室门禁系统_1_out_5 , \小型实验室门禁系统_1_out_6 , \小型实验室门禁系统_1_out_7 , \小型实验室门禁系统_1_out_8 ,
       \小型实验室门禁系统_1_out_9 , \小型实验室门禁系统_1_out_10 , \小型实验室门禁系统_1_out_11 , \小型实验室门禁系统_1_out_12 ,
       \小型实验室门禁系统_1_out_13 , \小型实验室门禁系统_1_out_14 , \小型实验室门禁系统_1_out_15 , \小型实验室门禁系统_1_out_16 ,
       \小型实验室门禁系统_1_out_17 , \小型实验室门禁系统_1_out_18 ;

  \小型实验室门禁系统  \u_小型实验室门禁系统_1  (
    .CPu(CPu), .CPd(CPd), .CLR(CLR), .ERROR(ERROR), .out_5(\小型实验室门禁系统_1_out_5 ), .out_6(\小型实验室门禁系统_1_out_6 ),
    .out_7(\小型实验室门禁系统_1_out_7 ), .out_8(\小型实验室门禁系统_1_out_8 ), .out_9(\小型实验室门禁系统_1_out_9 ),
    .out_10(\小型实验室门禁系统_1_out_10 ), .out_11(\小型实验室门禁系统_1_out_11 ), .out_12(\小型实验室门禁系统_1_out_12 ),
    .out_13(\小型实验室门禁系统_1_out_13 ), .out_14(\小型实验室门禁系统_1_out_14 ), .out_15(\小型实验室门禁系统_1_out_15 ),
    .out_16(\小型实验室门禁系统_1_out_16 ), .out_17(\小型实验室门禁系统_1_out_17 ), .out_18(\小型实验室门禁系统_1_out_18 ));
  _7_Segment_Display #(.active("true")) u_7_segment_display_1 (
    .g(\小型实验室门禁系统_1_out_11 ), .f(\小型实验室门禁系统_1_out_10 ), .a(\小型实验室门禁系统_1_out_5 ), .b(\小型实验室门禁系统_1_out_6 ),
    .e(\小型实验室门禁系统_1_out_9 ), .d(\小型实验室门禁系统_1_out_8 ), .c(\小型实验室门禁系统_1_out_7 ));  // open: dp
  _7_Segment_Display #(.active("true")) u_7_segment_display_2 (
    .g(\小型实验室门禁系统_1_out_18 ), .f(\小型实验室门禁系统_1_out_17 ), .a(\小型实验室门禁系统_1_out_12 ), .b(\小型实验室门禁系统_1_out_13 ),
    .e(\小型实验室门禁系统_1_out_16 ), .d(\小型实验室门禁系统_1_out_15 ), .c(\小型实验室门禁系统_1_out_14 ));  // open: dp
endmodule

module \先行进位的并行加法器  (
  input  C0,
  input  A0,
  input  B0,
  input  A1,
  input  B1,
  input  A2,
  input  B2,
  input  A3,
  input  B3,
  output S0,
  output S1,
  output S2,
  output S3,
  output C4
);

  wire and_1_out, and_2_out, and_3_out, and_4_out, and_5_out, and_6_out, and_7_out, and_8_out, and_9_out,
       and_10_out, C1_out, C2_out, C3_out, P0_out, P1_out, P2_out, P3_out, Q0_out, Q1_out, Q2_out, Q3_out,
       xor_1_out, xor_2_out, xor_3_out, xor_4_out;

  and P0 (P0_out, A0, B0);
  or Q0 (Q0_out, A0, B0);
  and P1 (P1_out, A1, B1);
  or Q1 (Q1_out, B1, A1);
  and P2 (P2_out, A2, B2);
  or Q2 (Q2_out, B2, A2);
  and P3 (P3_out, A3, B3);
  or Q3 (Q3_out, B3, A3);
  and and_1 (and_1_out, C0, Q0_out);
  and and_2 (and_2_out, P0_out, Q1_out);
  and and_3 (and_3_out, C0, Q0_out, Q1_out);
  and and_4 (and_4_out, P1_out, Q2_out);
  and and_5 (and_5_out, Q2_out, Q1_out, P0_out);
  and and_6 (and_6_out, Q2_out, Q1_out, C0, Q0_out);
  and and_7 (and_7_out, P2_out, Q3_out);
  and and_8 (and_8_out, Q3_out, Q2_out, P1_out);
  and and_9 (and_9_out, P0_out, Q1_out, Q2_out, Q3_out);
  and and_10 (and_10_out, C0, Q0_out, Q1_out, Q2_out, Q3_out);
  or C1 (C1_out, P0_out, and_1_out);
  or C2 (C2_out, P1_out, and_2_out, and_3_out);
  or C3 (C3_out, P2_out, and_4_out, and_5_out, and_6_out);
  or u_C4 (C4, P3_out, and_7_out, and_8_out, and_9_out, and_10_out);
  xor xor_1 (xor_1_out, A0, B0);
  xor xor_2 (xor_2_out, A1, C1_out);
  xor xor_3 (xor_3_out, C2_out, A2);
  xor xor_4 (xor_4_out, C3_out, A3);
  xor xor_5 (S0, xor_1_out, C0);
  xor xor_6 (S1, xor_2_out, B1);
  xor xor_7 (S2, xor_3_out, B2);
  xor xor_8 (S3, xor_4_out, B3);
endmodule

module \_7段译码器  (
  input  A3,
  input  A2,
  input  A1,
  input  A0,
  output FA,
  output FB,
  output FC,
  output FD,
  output FE,
  output FF,
  output FG
);

  wire and_1_out, and_2_out, and_3_out, and_4_out, and_5_out, and_6_out, and_7_out, and_8_out, and_9_out,
       and_10_out, and_11_out, and_12_out, and_13_out, and_14_out, and_15_out, and_16_out, not_1_out,
       not_2_out, not_3_out, not_4_out, not_5_out, not_6_out, not_7_out, not_8_out, not_9_out, not_10_out,
       not_11_out, not_12_out, not_13_out, not_14_out, not_15_out, not_16_out, not_17_out, not_18_out,
       not_19_out, not_20_out, not_21_out;

  not not_1 (not_1_out, A2);
  and and_1 (and_1_out, not_1_out, not_2_out);
  not not_2 (not_2_out, A0);
  and and_2 (and_2_out, A2, A0);
  not not_3 (not_3_out, A2);
  not not_4 (not_4_out, A1);
  and and_3 (and_3_out, not_4_out, not_5_out);
  not not_5 (not_5_out, A0);
  and and_4 (and_4_out, A1, A0);
  not not_6 (not_6_out, A1);
  or or_1 (FC, not_6_out, A0, A2);
  not not_7 (not_7_out, A2);
  and and_5 (and_5_out, not_7_out, not_8_out);
  not not_8 (not_8_out, A0);
  not not_9 (not_9_out, A2);
  and and_6 (and_6_out, not_9_out, A1);
  and and_7 (and_7_out, A1, not_10_out);
  not not_10 (not_10_out, A0);
  not not_11 (not_11_out, A1);
  and and_8 (and_8_out, A2, not_11_out, A0);
  not not_12 (not_12_out, A2);
  and and_9 (and_9_out, not_12_out, not_13_out);
  not not_13 (not_13_out, A0);
  and and_10 (and_10_out, A1, not_14_out);
  not not_14 (not_14_out, A0);
  not not_15 (not_15_out, A1);
  and and_11 (and_11_out, not_15_out, not_16_out);
  not not_16 (not_16_out, A0);
  and and_12 (and_12_out, A2, not_17_out);
  not not_17 (not_17_out, A1);
  and and_13 (and_13_out, A2, not_18_out);
  not not_18 (not_18_out, A0);
  not not_19 (not_19_out, A2);
  and and_14 (and_14_out, not_19_out, A1);
  and and_15 (and_15_out, A2, not_20_out);
  not not_20 (not_20_out, A1);
  and and_16 (and_16_out, A2, not_21_out);
  not not_21 (not_21_out, A0);
  or or_2 (FA, and_1_out, A1, and_2_out, A3);
  or or_3 (FB, not_3_out, and_3_out, and_4_out);
  or or_4 (FD, and_5_out, and_6_out, and_7_out, and_8_out, A3);
  or or_5 (FE, and_9_out, and_10_out);
  or or_6 (FF, and_11_out, and_12_out, and_13_out, A3);
  or or_7 (FG, and_14_out, and_15_out, and_16_out, A3);
endmodule
