// Logisim project 除法器.circ as structural Verilog: 5 circuits, main circuit 四位除法器
// div4
module \四位除法器  (
  input  [3:0] n2,
  input  [3:0] d,
  output [3:0] quot,
  output [3:0] rem
);

  wire comparator_1_lt, comparator_2_lt, comparator_3_lt, comparator_4_lt;
  wire [7:0] adder_1_out, adder_2_out, adder_3_out, adder_4_out, bit_extender_1_out, bit_extender_2_out,
       multiplexer_1_out, multiplexer_2_out, multiplexer_3_out, shifter_1_out, shifter_2_out, shifter_3_out,
       shifter_4_out, shifter_5_out, subtractor_1_out, subtractor_2_out, subtractor_3_out, subtractor_4_out;

  assign bit_extender_1_out = {{4{1'b0}}, n2};  // Bit_Extender bit_extender_1
  assign bit_extender_2_out = {{4{1'b0}}, d};  // Bit_Extender bit_extender_2
  Shifter #(.width(8), .shift("ll")) shifter_1 (.in(bit_extender_1_out), .\dist (3'b001), .out(shifter_1_out));
  Shifter #(.width(8), .shift("ll")) shifter_2 (.in(bit_extender_2_out), .\dist (3'b100), .out(shifter_2_out));
  Adder #(.width(8)) adder_1 (.a(shifter_1_out), .b(8'h1), .out(adder_1_out));  // open: cin, cout
  Comparator #(.width(8), .mode("unsigned")) comparator_1 (
    .a(shifter_1_out), .b(shifter_2_out), .lt(comparator_1_lt));  // open: gt, eq
  Subtractor #(.width(8)) subtractor_1 (.a(adder_1_out), .b(shifter_2_out), .out(subtractor_1_out));  // open: bin, bout
  Multiplexer #(.select(1), .width(8), .disabled("Z"), .enable("false")) multiplexer_1 (
    .in0(subtractor_1_out), .in1(shifter_1_out), .out(multiplexer_1_out), .sel(comparator_1_lt));
  Shifter #(.width(8), .shift("ll")) shifter_3 (.in(multiplexer_1_out), .\dist (3'b001), .out(shifter_3_out));
  Comparator #(.width(8), .mode("unsigned")) comparator_2 (
    .a(shifter_3_out), .b(shifter_2_out), .lt(comparator_2_lt));  // open: gt, eq
  Adder #(.width(8)) adder_2 (.a(shifter_3_out), .b(8'h1), .out(adder_2_out));  // open: cin, cout
  Subtractor #(.width(8)) subtractor_2 (.a(adder_2_out), .b(shifter_2_out), .out(subtractor_2_out));  // open: bin, bout
  Multiplexer #(.select(1), .width(8), .disabled("Z"), .enable("false")) multiplexer_2 (
    .in0(subtractor_2_out), .in1(shifter_3_out), .out(multiplexer_2_out), .sel(comparator_2_lt));
  Shifter #(.width(8), .shift("ll")) shifter_4 (.in(multiplexer_2_out), .\dist (3'b001), .out(shifter_4_out));
  Comparator #(.width(8), .mode("unsigned")) comparator_3 (
    .a(shifter_4_out), .b(shifter_2_out), .lt(comparator_3_lt));  // open: gt, eq
  Adder #(.width(8)) adder_3 (.a(shifter_4_out), .b(8'h1), .out(adder_3_out));  // open: cin, cout
  Subtractor #(.width(8)) subtractor_3 (.a(adder_3_out), .b(shifter_2_out), .out(subtractor_3_out));  // open: bin, bout
  Multiplexer #(.select(1), .width(8), .disabled("Z"), .enable("false")) multiplexer_3 (
    .in0(subtractor_3_out), .in1(shifter_4_out), .out(multiplexer_3_out), .sel(comparator_3_lt));
  Shifter #(.width(8), .shift("ll")) shifter_5 (.in(multiplexer_3_out), .\dist (3'b001), .out(shifter_5_out));
  Comparator #(.width(8), .mode("unsigned")) comparator_4 (
    .a(shifter_5_out), .b(shifter_2_out), .lt(comparator_4_lt));  // open: gt, eq
  Adder #(.width(8)) adder_4 (.a(shifter_5_out), .b(8'h1), .out(adder_4_out));  // open: cin, cout
  Subtractor #(.width(8)) subtractor_4 (.a(adder_4_out), .b(shifter_2_out), .out(subtractor_4_out));  // open: bin, bout
  Multiplexer #(.select(1), .width(8), .disabled("Z"), .enable("false")) multiplexer_4 (
    .in0(subtractor_4_out), .in1(shifter_5_out), .out({rem, quot}), .sel(comparator_4_lt));
endmodule

module \四位除法器测试电路  (
  input  [3:0] n2,
  input  [3:0] d,
  output [3:0] quot,
  output [3:0] rem
);

  \四位除法器  \u_四位除法器_1  (.n2(n2), .d(d), .quot(quot), .rem(rem));
endmodule

module \_32位除法器  (
  input  [31:0] n2,
  input  [31:0] d,
  output [31:0] quot,
  output [31:0] rem
);

  wire [31:0] \单个模块_1_n1_2 , \单个模块_1_n2_2 , \单个模块_1_out_6 , \单个模块_2_n1_2 , \单个模块_2_n2_2 , \单个模块_2_out_6 ,
       \单个模块_3_n1_2 , \单个模块_3_n2_2 , \单个模块_3_out_6 , \单个模块_4_n1_2 , \单个模块_4_n2_2 , \单个模块_4_out_6 ,
       \单个模块_5_n1_2 , \单个模块_5_n2_2 , \单个模块_5_out_6 , \单个模块_6_n1_2 , \单个模块_6_n2_2 , \单个模块_6_out_6 ,
       \单个模块_7_n1_2 , \单个模块_7_n2_2 , \单个模块_7_out_6 , \单个模块_8_n1_2 , \单个模块_8_n2_2 , \单个模块_8_out_6 ,
       \单个模块_9_n1_2 , \单个模块_9_n2_2 , \单个模块_9_out_6 , \单个模块_10_n1_2 , \单个模块_10_n2_2 , \单个模块_10_out_6 ,
       \单个模块_11_n1_2 , \单个模块_11_n2_2 , \单个模块_11_out_6 , \单个模块_12_n1_2 , \单个模块_12_n2_2 , \单个模块_12_out_6 ,
       \单个模块_13_n1_2 , \单个模块_13_n2_2 , \单个模块_13_out_6 , \单个模块_14_n1_2 , \单个模块_14_n2_2 , \单个模块_14_out_6 ,
       \单个模块_15_n1_2 , \单个模块_15_n2_2 , \单个模块_15_out_6 , \单个模块_16_n1_2 , \单个模块_16_n2_2 , \单个模块_16_out_6 ,
       \单个模块_17_n1_2 , \单个模块_17_n2_2 , \单个模块_17_out_6 , \单个模块_18_n1_2 , \单个模块_18_n2_2 , \单个模块_18_out_6 ,
       \单个模块_19_n1_2 , \单个模块_19_n2_2 , \单个模块_19_out_6 , \单个模块_20_n1_2 , \单个模块_20_n2_2 , \单个模块_20_out_6 ,
       \单个模块_21_n1_2 , \单个模块_21_n2_2 , \单个模块_21_out_6 , \单个模块_23_n1_2 , \单个模块_23_n2_2 , \单个模块_23_out_6 ,
       \单个模块_24_n1_2 , \单个模块_24_n2_2 , \单个模块_24_out_6 , \单个模块_25_n1_2 , \单个模块_25_n2_2 , \单个模块_25_out_6 ,
       \单个模块_26_n1_2 , \单个模块_26_n2_2 , \单个模块_26_out_6 , \单个模块_27_n1_2 , \单个模块_27_n2_2 , \单个模块_27_out_6 ,
       \单个模块_28_n1_2 , \单个模块_28_n2_2 , \单个模块_28_out_6 , \单个模块_29_n1_2 , \单个模块_29_n2_2 , \单个模块_29_out_6 ,
       \单个模块_30_n1_2 , \单个模块_30_n2_2 , \单个模块_30_out_6 , \单个模块_31_n1_2 , \单个模块_31_n2_2 , \单个模块_31_out_6 ,
       \单个模块_32_n1_2 , \单个模块_32_n2_2 , \单个模块_32_out_6 ;

  \单个模块  \u_单个模块_1  (
    .n2(\单个模块_12_n2_2 ), .n1(\单个模块_12_n1_2 ), .d(\单个模块_12_out_6 ), .n2_2(\单个模块_1_n2_2 ),
    .n1_2(\单个模块_1_n1_2 ), .out_6(\单个模块_1_out_6 ));
  \单个模块  \u_单个模块_2  (
    .n2(\单个模块_13_n2_2 ), .n1(\单个模块_13_n1_2 ), .d(\单个模块_13_out_6 ), .n2_2(\单个模块_2_n2_2 ),
    .n1_2(\单个模块_2_n1_2 ), .out_6(\单个模块_2_out_6 ));
  \单个模块  \u_单个模块_3  (
    .n2(\单个模块_14_n2_2 ), .n1(\单个模块_14_n1_2 ), .d(\单个模块_14_out_6 ), .n2_2(\单个模块_3_n2_2 ),
    .n1_2(\单个模块_3_n1_2 ), .out_6(\单个模块_3_out_6 ));
  \单个模块  \u_单个模块_4  (
    .n2(\单个模块_15_n2_2 ), .n1(\单个模块_15_n1_2 ), .d(\单个模块_15_out_6 ), .n2_2(\单个模块_4_n2_2 ),
    .n1_2(\单个模块_4_n1_2 ), .out_6(\单个模块_4_out_6 ));
  \单个模块  \u_单个模块_5  (
    .n2(\单个模块_16_n2_2 ), .n1(\单个模块_16_n1_2 ), .d(\单个模块_16_out_6 ), .n2_2(\单个模块_5_n2_2 ),
    .n1_2(\单个模块_5_n1_2 ), .out_6(\单个模块_5_out_6 ));
  \单个模块  \u_单个模块_6  (
    .n2(n2), .n1({32{1'b0}}), .d(d), .n2_2(\单个模块_6_n2_2 ), .n1_2(\单个模块_6_n1_2 ), .out_6(\单个模块_6_out_6 ));
  \单个模块  \u_单个模块_7  (
    .n2(\单个模块_1_n2_2 ), .n1(\单个模块_1_n1_2 ), .d(\单个模块_1_out_6 ), .n2_2(\单个模块_7_n2_2 ), .n1_2(\单个模块_7_n1_2 ),
    .out_6(\单个模块_7_out_6 ));
  \单个模块  \u_单个模块_8  (
    .n2(\单个模块_2_n2_2 ), .n1(\单个模块_2_n1_2 ), .d(\单个模块_2_out_6 ), .n2_2(\单个模块_8_n2_2 ), .n1_2(\单个模块_8_n1_2 ),
    .out_6(\单个模块_8_out_6 ));
  \单个模块  \u_单个模块_9  (
    .n2(\单个模块_3_n2_2 ), .n1(\单个模块_3_n1_2 ), .d(\单个模块_3_out_6 ), .n2_2(\单个模块_9_n2_2 ), .n1_2(\单个模块_9_n1_2 ),
    .out_6(\单个模块_9_out_6 ));
  \单个模块  \u_单个模块_10  (
    .n2(\单个模块_4_n2_2 ), .n1(\单个模块_4_n1_2 ), .d(\单个模块_4_out_6 ), .n2_2(\单个模块_10_n2_2 ), .n1_2(\单个模块_10_n1_2 ),
    .out_6(\单个模块_10_out_6 ));
  \单个模块  \u_单个模块_11  (
    .n2(\单个模块_5_n2_2 ), .n1(\单个模块_5_n1_2 ), .d(\单个模块_5_out_6 ), .n2_2(\单个模块_11_n2_2 ), .n1_2(\单个模块_11_n1_2 ),
    .out_6(\单个模块_11_out_6 ));
  \单个模块  \u_单个模块_12  (
    .n2(\单个模块_23_n2_2 ), .n1(\单个模块_23_n1_2 ), .d(\单个模块_23_out_6 ), .n2_2(\单个模块_12_n2_2 ),
    .n1_2(\单个模块_12_n1_2 ), .out_6(\单个模块_12_out_6 ));
  \单个模块  \u_单个模块_13  (
    .n2(\单个模块_24_n2_2 ), .n1(\单个模块_24_n1_2 ), .d(\单个模块_24_out_6 ), .n2_2(\单个模块_13_n2_2 ),
    .n1_2(\单个模块_13_n1_2 ), .out_6(\单个模块_13_out_6 ));
  \单个模块  \u_单个模块_14  (
    .n2(\单个模块_25_n2_2 ), .n1(\单个模块_25_n1_2 ), .d(\单个模块_25_out_6 ), .n2_2(\单个模块_14_n2_2 ),
    .n1_2(\单个模块_14_n1_2 ), .out_6(\单个模块_14_out_6 ));
  \单个模块  \u_单个模块_15  (
    .n2(\单个模块_26_n2_2 ), .n1(\单个模块_26_n1_2 ), .d(\单个模块_26_out_6 ), .n2_2(\单个模块_15_n2_2 ),
    .n1_2(\单个模块_15_n1_2 ), .out_6(\单个模块_15_out_6 ));
  \单个模块  \u_单个模块_16  (
    .n2(\单个模块_27_n2_2 ), .n1(\单个模块_27_n1_2 ), .d(\单个模块_27_out_6 ), .n2_2(\单个模块_16_n2_2 ),
    .n1_2(\单个模块_16_n1_2 ), .out_6(\单个模块_16_out_6 ));
  \单个模块  \u_单个模块_17  (
    .n2(\单个模块_6_n2_2 ), .n1(\单个模块_6_n1_2 ), .d(\单个模块_6_out_6 ), .n2_2(\单个模块_17_n2_2 ), .n1_2(\单个模块_17_n1_2 ),
    .out_6(\单个模块_17_out_6 ));
  \单个模块  \u_单个模块_18  (
    .n2(\单个模块_7_n2_2 ), .n1(\单个模块_7_n1_2 ), .d(\单个模块_7_out_6 ), .n2_2(\单个模块_18_n2_2 ), .n1_2(\单个模块_18_n1_2 ),
    .out_6(\单个模块_18_out_6 ));
  \单个模块  \u_单个模块_19  (
    .n2(\单个模块_8_n2_2 ), .n1(\单个模块_8_n1_2 ), .d(\单个模块_8_out_6 ), .n2_2(\单个模块_19_n2_2 ), .n1_2(\单个模块_19_n1_2 ),
    .out_6(\单个模块_19_out_6 ));
  \单个模块  \u_单个模块_20  (
    .n2(\单个模块_9_n2_2 ), .n1(\单个模块_9_n1_2 ), .d(\单个模块_9_out_6 ), .n2_2(\单个模块_20_n2_2 ), .n1_2(\单个模块_20_n1_2 ),
    .out_6(\单个模块_20_out_6 ));
  \单个模块  \u_单个模块_21  (
    .n2(\单个模块_10_n2_2 ), .n1(\单个模块_10_n1_2 ), .d(\单个模块_10_out_6 ), .n2_2(\单个模块_21_n2_2 ),
    .n1_2(\单个模块_21_n1_2 ), .out_6(\单个模块_21_out_6 ));
  \单个模块  \u_单个模块_22  (
    .n2(\单个模块_11_n2_2 ), .n1(\单个模块_11_n1_2 ), .d(\单个模块_11_out_6 ), .n2_2(quot), .n1_2(rem));  // open: out_6
  \单个模块  \u_单个模块_23  (
    .n2(\单个模块_28_n2_2 ), .n1(\单个模块_28_n1_2 ), .d(\单个模块_28_out_6 ), .n2_2(\单个模块_23_n2_2 ),
    .n1_2(\单个模块_23_n1_2 ), .out_6(\单个模块_23_out_6 ));
  \单个模块  \u_单个模块_24  (
    .n2(\单个模块_29_n2_2 ), .n1(\单个模块_29_n1_2 ), .d(\单个模块_29_out_6 ), .n2_2(\单个模块_24_n2_2 ),
    .n1_2(\单个模块_24_n1_2 ), .out_6(\单个模块_24_out_6 ));
  \单个模块  \u_单个模块_25  (
    .n2(\单个模块_30_n2_2 ), .n1(\单个模块_30_n1_2 ), .d(\单个模块_30_out_6 ), .n2_2(\单个模块_25_n2_2 ),
    .n1_2(\单个模块_25_n1_2 ), .out_6(\单个模块_25_out_6 ));
  \单个模块  \u_单个模块_26  (
    .n2(\单个模块_31_n2_2 ), .n1(\单个模块_31_n1_2 ), .d(\单个模块_31_out_6 ), .n2_2(\单个模块_26_n2_2 ),
    .n1_2(\单个模块_26_n1_2 ), .out_6(\单个模块_26_out_6 ));
  \单个模块  \u_单个模块_27  (
    .n2(\单个模块_32_n2_2 ), .n1(\单个模块_32_n1_2 ), .d(\单个模块_32_out_6 ), .n2_2(\单个模块_27_n2_2 ),
    .n1_2(\单个模块_27_n1_2 ), .out_6(\单个模块_27_out_6 ));
  \单个模块  \u_单个模块_28  (
    .n2(\单个模块_17_n2_2 ), .n1(\单个模块_17_n1_2 ), .d(\单个模块_17_out_6 ), .n2_2(\单个模块_28_n2_2 ),
    .n1_2(\单个模块_28_n1_2 ), .out_6(\单个模块_28_out_6 ));
  \单个模块  \u_单个模块_29  (
    .n2(\单个模块_18_n2_2 ), .n1(\单个模块_18_n1_2 ), .d(\单个模块_18_out_6 ), .n2_2(\单个模块_29_n2_2 ),
    .n1_2(\单个模块_29_n1_2 ), .out_6(\单个模块_29_out_6 ));
  \单个模块  \u_单个模块_30  (
    .n2(\单个模块_19_n2_2 ), .n1(\单个模块_19_n1_2 ), .d(\单个模块_19_out_6 ), .n2_2(\单个模块_30_n2_2 ),
    .n1_2(\单个模块_30_n1_2 ), .out_6(\单个模块_30_out_6 ));
  \单个模块  \u_单个模块_31  (
    .n2(\单个模块_20_n2_2 ), .n1(\单个模块_20_n1_2 ), .d(\单个模块_20_out_6 ), .n2_2(\单个模块_31_n2_2 ),
    .n1_2(\单个模块_31_n1_2 ), .out_6(\单个模块_31_out_6 ));
  \单个模块  \u_单个模块_32  (
    .n2(\单个模块_21_n2_2 ), .n1(\单个模块_21_n1_2 ), .d(\单个模块_21_out_6 ), .n2_2(\单个模块_32_n2_2 ),
    .n1_2(\单个模块_32_n1_2 ), .out_6(\单个模块_32_out_6 ));
endmodule

module \_32位除法器测试电路  (
  input  [31:0] n2,
  input  [31:0] d,
  output [31:0] quot,
  output [31:0] rem
);

  \_32位除法器  \u_32位除法器_1  (.n2(n2), .d(d), .quot(quot), .rem(rem));
endmodule

module \单个模块  (
  input  [31:0] n2,
  input  [31:0] n1,
  input  [31:0] d,
  output [31:0] n2_2,
  output [31:0] n1_2,
  output [31:0] out_6
);

  wire comparator_1_lt;
  wire [31:0] adder_1_out, adder_2_out, shifter_1_out, shifter_2_out, shifter_3_out, subtractor_1_out;

  Shifter #(.width(32), .shift("lr")) shifter_1 (.in(n2), .\dist ({5{1'b1}}), .out(shifter_1_out));
  Shifter #(.width(32), .shift("ll")) shifter_2 (.in(n1), .\dist (5'b00001), .out(shifter_2_out));
  Shifter #(.width(32), .shift("ll")) shifter_3 (.in(n2), .\dist (5'b00001), .out(shifter_3_out));
  Adder #(.width(32)) adder_1 (.a(shifter_1_out), .b(shifter_2_out), .out(adder_1_out));  // open: cin, cout
  Comparator #(.width(32), .mode("unsigned")) comparator_1 (
    .a(adder_1_out), .b(d), .lt(comparator_1_lt));  // open: gt, eq
  Adder #(.width(32)) adder_2 (.a(shifter_3_out), .b(32'h1), .out(adder_2_out));  // open: cin, cout
  Multiplexer #(.select(1), .width(32), .disabled("Z"), .enable("false")) multiplexer_1 (
    .in0(adder_2_out), .in1(shifter_3_out), .out(n2_2), .sel(comparator_1_lt));
  Subtractor #(.width(32)) subtractor_1 (.a(adder_1_out), .b(d), .out(subtractor_1_out));  // open: bin, bout
  Multiplexer #(.select(1), .width(32), .disabled("Z"), .enable("false")) multiplexer_2 (
    .in0(subtractor_1_out), .in1(adder_1_out), .out(n1_2), .sel(comparator_1_lt));

  assign out_6 = d;
endmodule
